// Logisim project Control_Unit.circ as structural Verilog: 6 circuits, main circuit Control Unit
module Control_Unit (
  input  END_CS_IN,
  input  RST,
  input  CLK,
  input  [5:0] Func_Code,
  input  [5:0] OP_Code,
  input  Flag,
  output out_7,
  output CS,
  output TTY_ENABLE,
  output [3:0] ALU_SEL,
  output [1:0] ALUB,
  output ALUA,
  output [2:0] RFInput,
  output [1:0] RF_SEL,
  output [1:0] BCSelector,
  output [2:0] FlagSelector,
  output writeRF,
  output writePC,
  output \unsigned ,
  output [1:0] MA_SEL,
  output DOut_SEL,
  output RAM_RW,
  output DIn_SEL,
  output KBD_EN
);

  wire _1_Cycle_q, add, addi, ALUA_pop, ALUA_SEL_Imm, ALUA_stack, \and , andi, beq, bgtz, blez, bltz, bne,
       branch, BranchEnd, CS_EN_Instruction, CS_EN_pop, CS_EN_push, CS_EN_stack, demultiplexer_1_out0,
       demultiplexer_1_out1, demultiplexer_2_out1, div, divu, halt, haltOut, IDLE_q, immediate, ImmEnd, jr,
       load_Word, LoadEnd, mfhi, mflo, mul, mulu, n1_bit_demultiplexer_1_o0, n1_bit_demultiplexer_2_o1,
       n1_bit_demultiplexer_3_o0, n1_bit_demultiplexer_4_o1, n1_bit_demultiplexer_5_o0,
       n1_bit_demultiplexer_5_o1, n1_bit_demultiplexer_6_o0, n1_bit_demultiplexer_6_o1,
       n1_bit_demultiplexer_9_o1, next, \nor , not_1_out, not_2_out, not_3_out, not_4_out, not_5_out, \or ,
       or_1_out, or_2_out, or_3_out, or_5_out, or_7_out, or_10_out, or_11_out, or_17_out, ori, push_tty, rnd,
       slt, slti, sltiu, sltu, special, SpecialEnd, stack, StackEnd, stBranch, stImm, stLoad_Word,
       store_Word, StoreEnd, stSpecial, stStack, stStore_Word, stZero, sub, WAIT_READ_2_q, WAIT_READ_q,
       WRITE_RF_Imm, WRITE_RF_Zero, WritePC_Imm, WritePC_stack, WritePC_Store, WritePC_Zero, WRTE_RF_stack,
       \xor , xori, zero, ZeroEnd;
  wire [0:0] ALU_SEL_push, ALUB_SEL_Load, BC_SEL_Branch, RF_Input_pop;
  wire [1:0] ALUB_SEL_Imm, ALUB_stack, BC_SEL_Imm, BC_SEL_Zero, MA_SEL_stack, or_21_out, RF_SEL_Imm,
       RF_SEL_Zero;
  wire [1:1] RF_SEL_Load, RF_SEL_rnd_kbd;
  wire [2:0] Flag_SEL, RF_Input_Imm, RF_Input_Zero;
  wire [2:2] RF_Input_rnd;
  wire [3:0] ALU_SEL_Imm, ALU_SEL_Zero;

  _1_bit_Demultiplexer u_1_bit_demultiplexer_1 (
    .i(stStack), .S(push_tty), .o0(n1_bit_demultiplexer_1_o0), .o1(ALU_SEL_push[0]));
  Op_Code_Decoder op_code_decoder_1 (
    .o0(OP_Code[0]), .o1(OP_Code[1]), .o2(OP_Code[2]), .o3(OP_Code[3]), .o4(OP_Code[4]), .o5(OP_Code[5]),
    .zero(zero), .beq(beq), .special(special), .addi(addi), .bne(bne), .andi(andi), .blez(blez), .ori(ori),
    .bgtz(bgtz), .xori(xori), .lw(load_Word), .slti(slti), .sw(store_Word), .sltiu(sltiu), .stack(stack),
    .bltz(bltz), .ENABLE(1'b1));
  Func_Code_Decoder func_code_decoder_1 (
    .f0(Func_Code[0]), .f1(Func_Code[1]), .f2(Func_Code[2]), .f3(Func_Code[3]), .f4(Func_Code[4]),
    .f5(Func_Code[5]), .EN(1'b1), .add(add), .\and (\and ), .sub(sub), .\or (\or ), .push_tty(push_tty),
    .mul(mul), .\nor (\nor ), .halt(halt), .mulu(mulu), .\xor (\xor ), .rnd(rnd), .div(div), .mfhi(mfhi),
    .mflo(mflo), .divu(divu), .slt(slt), .jr(jr), .sltu(sltu));  // open: nop_pop, kbd
  or or_1 (or_1_out, stStore_Word, DOut_SEL);
  _1_bit_Demultiplexer u_1_bit_demultiplexer_2 (
    .i(or_1_out), .S(not_1_out), .o0(WritePC_Store), .o1(n1_bit_demultiplexer_2_o1));
  not not_1 (not_1_out, END_CS_IN);
  or or_2 (or_2_out, n1_bit_demultiplexer_1_o0, CS_EN_pop);
  _1_bit_Demultiplexer u_1_bit_demultiplexer_3 (
    .i(stBranch), .S(Flag), .o0(n1_bit_demultiplexer_3_o0), .o1(BC_SEL_Branch[0]));
  Branch_Mapper branch_mapper_1 (.beq(beq), .bne(bne), .blez(blez), .bgtz(bgtz), .bltz(bltz), .Flag_Sel(Flag_SEL));
  _1_bit_Demultiplexer u_1_bit_demultiplexer_4 (
    .i(or_2_out), .S(not_2_out), .o0(RF_Input_pop[0]), .o1(n1_bit_demultiplexer_4_o1));
  not not_2 (not_2_out, END_CS_IN);
  D_Flip_Flop _1_Cycle (.clk(CLK), .D(ALU_SEL_push[0]), .Q(_1_Cycle_q), .reset(RST));  // open: Qn, preset, en
  D_Flip_Flop IDLE (.clk(CLK), .D(demultiplexer_1_out1), .Q(IDLE_q), .preset(RST));  // open: Qn, en, reset
  D_Flip_Flop _1_Cycle_2 (.clk(CLK), .D(WritePC_Store), .Q(StoreEnd), .reset(RST));  // open: Qn, preset, en
  D_Flip_Flop WAIT (.clk(CLK), .D(n1_bit_demultiplexer_2_o1), .Q(DOut_SEL), .reset(RST));  // open: Qn, preset, en
  D_Flip_Flop WAIT_2 (.clk(CLK), .D(n1_bit_demultiplexer_4_o1), .Q(CS_EN_pop), .reset(RST));  // open: Qn, preset, en
  or or_3 (or_3_out, _1_Cycle_q, CS_EN_push);
  _1_bit_Demultiplexer u_1_bit_demultiplexer_5 (
    .i(or_3_out), .S(not_3_out), .o0(n1_bit_demultiplexer_5_o0), .o1(n1_bit_demultiplexer_5_o1));
  not not_3 (not_3_out, END_CS_IN);
  Demultiplexer demultiplexer_1 (
    .out0(demultiplexer_1_out0), .out1(demultiplexer_1_out1), .in(IDLE_q), .sel(RST));  // open: en
  or or_4 (branch, beq, bne, blez, bgtz, bltz);
  or or_5 (or_5_out, n1_bit_demultiplexer_3_o0, BC_SEL_Branch[0]);
  or or_6 (CS_EN_Instruction, next, demultiplexer_1_out0);
  D_Flip_Flop _1_CYCLE_3 (.clk(CLK), .D(or_5_out), .Q(BranchEnd), .reset(RST));  // open: Qn, preset, en
  D_Flip_Flop _1_Cycle_4 (.clk(CLK), .D(RF_Input_pop[0]), .Q(ALUA_pop), .reset(RST));  // open: Qn, preset, en
  D_Flip_Flop WAIT_3 (.clk(CLK), .D(n1_bit_demultiplexer_5_o1), .Q(CS_EN_push), .reset(RST));  // open: Qn, preset, en
  or or_7 (or_7_out, CS_EN_Instruction, WAIT_READ_q);
  Demultiplexer demultiplexer_2 (
    .out0(out_7), .out1(demultiplexer_2_out1), .in(or_7_out), .sel(not_4_out));  // open: en
  _1_bit_Demultiplexer u_1_bit_demultiplexer_6 (
    .i(stSpecial), .S(halt), .o0(n1_bit_demultiplexer_6_o0), .o1(n1_bit_demultiplexer_6_o1));
  or or_8 (WritePC_stack, ALUA_pop, n1_bit_demultiplexer_5_o0);
  not not_4 (not_4_out, END_CS_IN);
  or or_9 (immediate, addi, andi, ori, xori, slti, sltiu);
  _1_bit_Demultiplexer u_1_bit_demultiplexer_7 (
    .i(n1_bit_demultiplexer_6_o0), .S(push_tty), .o0(RF_SEL_rnd_kbd[1]), .o1(TTY_ENABLE));
  D_Flip_Flop _1_Cycle_5 (.clk(CLK), .D(WritePC_stack), .Q(StackEnd), .reset(RST));  // open: Qn, preset, en
  D_Flip_Flop WAIT_READ (.clk(CLK), .D(demultiplexer_2_out1), .Q(WAIT_READ_q), .reset(RST));  // open: Qn, preset, en
  ZeroMapper zeromapper_1 (
    .EN(stZero), .add(add), .sub(sub), .mul(mul), .mulu(mulu), .div(div), .divu(divu), .\and (\and ),
    .\or (\or ), .\nor (\nor ), .\xor (\xor ), .mfhi(mfhi), .mflo(mflo), .jr(jr), .slt(slt), .sltu(sltu),
    .WritePC(WritePC_Zero), .ALU_SEL(ALU_SEL_Zero), .WriteRF(WRITE_RF_Zero), .RFInput(RF_Input_Zero),
    .Unsigned(\unsigned ), .RFSelector(RF_SEL_Zero), .BC_SEL(BC_SEL_Zero));
  D_Flip_Flop _1_CYCLE_6 (.clk(CLK), .D(stImm), .Q(ImmEnd), .reset(RST));  // open: Qn, preset, en
  I_Mapper i_mapper_1 (
    .EN(stImm), .addi(addi), .andi(andi), .ori(ori), .xori(xori), .slti(slti), .sltiu(sltiu),
    .WritePC(WritePC_Imm), .WriteRF(WRITE_RF_Imm), .ALUA(ALUA_SEL_Imm), .ALUB(ALUB_SEL_Imm),
    .RF_INPUT(RF_Input_Imm), .RF_SEL(RF_SEL_Imm), .BC_SEL(BC_SEL_Imm), .ALU_SEL(ALU_SEL_Imm));
  _1_bit_Demultiplexer u_1_bit_demultiplexer_8 (.i(RF_SEL_rnd_kbd[1]), .S(rnd), .o0(DIn_SEL), .o1(RF_Input_rnd[2]));
  D_Flip_Flop #(.trigger("high")) u_Halt (.clk(CLK), .D(or_10_out), .Q(haltOut), .reset(RST));  // open: Qn, preset, en
  or or_10 (or_10_out, n1_bit_demultiplexer_6_o1, haltOut);
  D_Flip_Flop WAIT_READ_2 (.clk(CLK), .D(out_7), .Q(WAIT_READ_2_q), .reset(RST));  // open: Qn, preset, en
  D_Flip_Flop _1_CYCLE_7 (.clk(CLK), .D(stZero), .Q(ZeroEnd), .reset(RST));  // open: Qn, preset, en
  _1_bit_Demultiplexer u_1_bit_demultiplexer_9 (
    .i(or_11_out), .S(not_5_out), .o0(RF_SEL_Load[1]), .o1(n1_bit_demultiplexer_9_o1));
  or or_11 (or_11_out, stLoad_Word, ALUB_SEL_Load[0]);
  not not_5 (not_5_out, END_CS_IN);
  and and_1 (stZero, WAIT_READ_2_q, zero);
  and and_2 (stImm, WAIT_READ_2_q, immediate);
  and and_3 (stBranch, WAIT_READ_2_q, branch);
  and and_4 (stLoad_Word, WAIT_READ_2_q, load_Word);
  and and_5 (stStore_Word, WAIT_READ_2_q, store_Word);
  D_Flip_Flop WAIT_4 (
    .clk(CLK), .D(n1_bit_demultiplexer_9_o1), .Q(ALUB_SEL_Load[0]), .reset(RST));  // open: Qn, preset, en
  or or_12 (ALUA_stack, ALUA_pop, ALU_SEL_push[0]);
  assign ALUB_stack = {2{ALUA_pop}} | {2{ALU_SEL_push[0]}};  // OR_Gate or_13, 2 bits wide
  or or_14 (CS_EN_stack, CS_EN_push, CS_EN_pop);
  assign MA_SEL_stack = {CS_EN_pop, 1'b0} | {CS_EN_push, 1'b0};  // OR_Gate or_15, 2 bits wide
  or or_16 (WRTE_RF_stack, RF_Input_pop[0], ALUA_pop, ALU_SEL_push[0]);
  or or_17 (or_17_out, DIn_SEL, RF_Input_rnd[2], TTY_ENABLE);
  and and_6 (stSpecial, WAIT_READ_2_q, special);
  and and_7 (stStack, WAIT_READ_2_q, stack);
  or or_18 (next, ZeroEnd, ImmEnd, BranchEnd, LoadEnd, StoreEnd, SpecialEnd, StackEnd);
  D_Flip_Flop _1_Cycle_8 (.clk(CLK), .D(RF_SEL_Load[1]), .Q(LoadEnd), .reset(RST));  // open: Qn, preset, en
  D_Flip_Flop _1_Cycle_9 (.clk(CLK), .D(or_17_out), .Q(SpecialEnd), .reset(RST));  // open: Qn, preset, en
  assign ALU_SEL = ALU_SEL_Zero | ALU_SEL_Imm | {3'b000, ALU_SEL_push[0]};  // OR_Gate or_19, 4 bits wide
  or or_20 (CS, CS_EN_Instruction, ALUB_SEL_Load[0], DOut_SEL, CS_EN_stack);
  assign or_21_out = ALUB_SEL_Imm | ALUB_stack | {1'b0, DOut_SEL} | {1'b0, ALUB_SEL_Load[0]};  // OR_Gate or_21, 2 bits wide
  or or_22 (ALUA, ALUA_SEL_Imm, ALUA_stack);
  assign RFInput = RF_Input_Zero | RF_Input_Imm | {2'b00, RF_SEL_Load[1]} | {2'b00, DIn_SEL} | {RF_Input_rnd[2], 2'b00} | {2'b00, RF_Input_pop[0]};  // OR_Gate or_23, 3 bits wide
  assign RF_SEL = RF_SEL_Zero | RF_SEL_Imm | {RF_Input_pop[0], 1'b0} | {RF_SEL_Load[1], 1'b0} | {RF_SEL_rnd_kbd[1], 1'b0};  // OR_Gate or_24, 2 bits wide
  assign BCSelector = BC_SEL_Zero | BC_SEL_Imm | {1'b0, BC_SEL_Branch[0]};  // OR_Gate or_25, 2 bits wide
  or or_26 (writeRF, WRITE_RF_Zero, WRITE_RF_Imm, RF_SEL_Load[1], RF_SEL_rnd_kbd[1], WRTE_RF_stack);
  or or_27 (writePC, WritePC_Zero, WritePC_Imm, stBranch, RF_SEL_Load[1], WritePC_Store, RF_SEL_rnd_kbd[1], TTY_ENABLE, WritePC_stack);
  assign MA_SEL = {1'b0, DOut_SEL} | {1'b0, ALUB_SEL_Load[0]} | MA_SEL_stack;  // OR_Gate or_28, 2 bits wide
  or or_29 (RAM_RW, DOut_SEL, CS_EN_push);

  assign KBD_EN = DIn_SEL;

  // Other names for the same wires on the sheet: ALU_SEL_stack[0] = ALU_SEL_push[0]; ALUA_push = ALU_SEL_push[0];
  //   ALUB_push[1:0] = {2{ALU_SEL_push[0]}}; WRITE_RF_push0 = ALU_SEL_push[0]; ALUB_pop[1:0] = {2{ALUA_pop}};
  //   WRITE_RF_pop1 = ALUA_pop; CS_EN_Load = ALUB_SEL_Load[0]; MA_SEL_Load[0] = ALUB_SEL_Load[0];
  //   MA_SEL_pop[1] = CS_EN_pop; MA_SEL_push[1] = CS_EN_push; RAM_RW_push = CS_EN_push; RAM_RW_stack = CS_EN_push;
  //   ALUB_SEL_Store[0] = DOut_SEL; CS_EN_Store = DOut_SEL; DOut_SEL_Store = DOut_SEL; MA_SEL_Store[0] = DOut_SEL;
  //   RAM_RW_store = DOut_SEL; DIn_SEL_kbd = DIn_SEL; RF_Input_kbd[0] = DIn_SEL; WRITE_RF_rnd_kbd = RF_SEL_rnd_kbd[1];
  //   WritePC_rnd_kbd = RF_SEL_rnd_kbd[1]; RF_Input_stack[0] = RF_Input_pop[0]; RF_SEL_pop[1] = RF_Input_pop[0];
  //   RF_SEL_stack[1] = RF_Input_pop[0]; WRITE_RF_pop0 = RF_Input_pop[0]; RFInput_Load[0] = RF_SEL_Load[1];
  //   WRITE_RF_Load = RF_SEL_Load[1]; WritePC_Load = RF_SEL_Load[1]; WritePC_Branch = stBranch; Write_ID = out_7;
  //   TTY_EN = TTY_ENABLE; WritePC_TTY = TTY_ENABLE

  // Notes on the sheet:
  //   kbd
endmodule

module Op_Code_Decoder (
  input  o0,
  input  o1,
  input  o2,
  input  o3,
  input  o4,
  input  o5,
  input  ENABLE,
  output zero,
  output beq,
  output stack,
  output addi,
  output bne,
  output special,
  output andi,
  output blez,
  output ori,
  output bgtz,
  output xori,
  output bltz,
  output slti,
  output lw,
  output sltiu,
  output sw
);

  wire and_1_out, and_2_out, and_3_out, and_4_out, and_5_out, and_6_out, and_7_out, and_15_out, and_16_out,
       and_17_out, and_18_out, and_19_out, and_20_out, and_21_out, and_29_out, and_30_out;

  and and_1 (and_1_out, ~o0, ~o1, ~o1, ~o3, ~o4, ~o5);  // AND_Gate
  and and_2 (and_2_out, ~o0, ~o1, ~o1, o3, ~o4, ~o5);  // AND_Gate
  and and_3 (and_3_out, ~o0, ~o1, o1, o3, ~o4, ~o5);  // AND_Gate
  and and_4 (and_4_out, o0, ~o1, o1, o3, ~o4, ~o5);  // AND_Gate
  and and_5 (and_5_out, ~o0, o1, o1, o3, ~o4, ~o5);  // AND_Gate
  and and_6 (and_6_out, ~o0, o1, ~o1, o3, ~o4, ~o5);  // AND_Gate
  and and_7 (and_7_out, o0, o1, ~o1, o3, ~o4, ~o5);  // AND_Gate
  and and_8 (zero, and_1_out, ENABLE);
  and and_9 (addi, and_2_out, ENABLE);
  and and_10 (andi, and_3_out, ENABLE);
  and and_11 (ori, and_4_out, ENABLE);
  and and_12 (xori, and_5_out, ENABLE);
  and and_13 (slti, and_6_out, ENABLE);
  and and_14 (sltiu, and_7_out, ENABLE);
  and and_15 (and_15_out, ~o0, ~o1, o1, ~o3, ~o4, ~o5);  // AND_Gate
  and and_16 (and_16_out, o0, ~o1, o1, ~o3, ~o4, ~o5);  // AND_Gate
  and and_17 (and_17_out, ~o0, o1, o1, ~o3, ~o4, ~o5);  // AND_Gate
  and and_18 (and_18_out, o0, o1, o1, ~o3, ~o4, ~o5);  // AND_Gate
  and and_19 (and_19_out, o0, ~o1, ~o1, ~o3, ~o4, ~o5);  // AND_Gate
  and and_20 (and_20_out, o0, o1, ~o1, ~o3, ~o4, o5);  // AND_Gate
  and and_21 (and_21_out, o0, o1, ~o1, o3, ~o4, o5);  // AND_Gate
  and and_22 (beq, and_15_out, ENABLE);
  and and_23 (bne, and_16_out, ENABLE);
  and and_24 (blez, and_17_out, ENABLE);
  and and_25 (bgtz, and_18_out, ENABLE);
  and and_26 (bltz, and_19_out, ENABLE);
  and and_27 (lw, and_20_out, ENABLE);
  and and_28 (sw, and_21_out, ENABLE);
  and and_29 (and_29_out, ~o0, ~o1, ~o1, o3, o4, o5);  // AND_Gate
  and and_30 (and_30_out, o0, o1, o1, o3, o4, o5);
  and and_31 (stack, and_29_out, ENABLE);
  and and_32 (special, and_30_out, ENABLE);

  assign o2 = o1;

  // Other names for the same wires on the sheet: EN = ENABLE
endmodule

module Func_Code_Decoder (
  input  f0,
  input  f1,
  input  f2,
  input  f3,
  input  f4,
  input  f5,
  input  EN,
  output nop_pop,
  output add,
  output \and ,
  output push_tty,
  output sub,
  output \or ,
  output halt,
  output mul,
  output \nor ,
  output rnd,
  output mulu,
  output \xor ,
  output kbd,
  output div,
  output mfhi,
  output mflo,
  output divu,
  output slt,
  output jr,
  output sltu
);

  wire and_1_out, and_2_out, and_3_out, and_4_out, and_5_out, and_6_out, and_7_out, and_8_out, and_17_out,
       and_18_out, and_19_out, and_20_out, and_21_out, and_22_out, and_23_out, and_31_out, and_32_out,
       and_33_out, and_34_out, and_35_out;

  and and_1 (and_1_out, ~f0, ~f1, ~f2, ~f3, ~f4, f5);  // AND_Gate
  and and_2 (and_2_out, ~f0, f1, ~f2, ~f3, ~f4, f5);  // AND_Gate
  and and_3 (and_3_out, ~f0, ~f1, ~f2, f3, f4, ~f5);  // AND_Gate
  and and_4 (and_4_out, f0, ~f1, ~f2, f3, f4, ~f5);  // AND_Gate
  and and_5 (and_5_out, ~f0, f1, ~f2, f3, f4, ~f5);  // AND_Gate
  and and_6 (and_6_out, f0, f1, ~f2, f3, f4, ~f5);  // AND_Gate
  and and_7 (and_7_out, ~f0, f1, ~f2, f3, ~f4, f5);  // AND_Gate
  and and_8 (and_8_out, f0, f1, ~f2, f3, ~f4, f5);  // AND_Gate
  and and_9 (add, and_1_out, EN);
  and and_10 (sub, and_2_out, EN);
  and and_11 (mul, and_3_out, EN);
  and and_12 (mulu, and_4_out, EN);
  and and_13 (div, and_5_out, EN);
  and and_14 (divu, and_6_out, EN);
  and and_15 (slt, and_7_out, EN);
  and and_16 (sltu, and_8_out, EN);
  and and_17 (and_17_out, ~f0, ~f1, f2, ~f3, ~f4, f5);  // AND_Gate
  and and_18 (and_18_out, f0, ~f1, f2, ~f3, ~f4, f5);  // AND_Gate
  and and_19 (and_19_out, f0, f1, f2, ~f3, ~f4, f5);  // AND_Gate
  and and_20 (and_20_out, ~f0, ~f1, ~f2, f3, ~f4, f5);  // AND_Gate
  and and_21 (and_21_out, ~f0, ~f1, ~f2, ~f3, f4, ~f5);  // AND_Gate
  and and_22 (and_22_out, ~f0, f1, ~f2, ~f3, f4, ~f5);  // AND_Gate
  and and_23 (and_23_out, ~f0, ~f1, ~f2, f3, ~f4, ~f5);  // AND_Gate
  and and_24 (\and , and_17_out, EN);
  and and_25 (\or , and_18_out, EN);
  and and_26 (\nor , and_19_out, EN);
  and and_27 (\xor , and_20_out, EN);
  and and_28 (mfhi, and_21_out, EN);
  and and_29 (mflo, and_22_out, EN);
  and and_30 (jr, and_23_out, EN);
  and and_31 (and_31_out, ~f0, ~f1, ~f2, ~f3, ~f4, ~f5);  // AND_Gate
  and and_32 (and_32_out, f0, ~f1, ~f2, ~f3, ~f4, ~f5);  // AND_Gate
  and and_33 (and_33_out, f0, f1, f2, f3, f4, f5);
  and and_34 (and_34_out, ~f0, f1, ~f2, ~f3, ~f4, ~f5);  // AND_Gate
  and and_35 (and_35_out, ~f0, ~f1, f2, ~f3, ~f4, ~f5);  // AND_Gate
  and and_36 (nop_pop, and_31_out, EN);
  and and_37 (push_tty, and_32_out, EN);
  and and_38 (halt, and_33_out, EN);
  and and_39 (rnd, and_34_out, EN);
  and and_40 (kbd, and_35_out, EN);
endmodule

module ZeroMapper (
  input  EN,
  input  add,
  input  sub,
  input  mul,
  input  mulu,
  input  div,
  input  divu,
  input  \and ,
  input  \or ,
  input  \nor ,
  input  \xor ,
  input  mfhi,
  input  mflo,
  input  jr,
  input  slt,
  input  sltu,
  output WritePC,
  output [3:0] ALU_SEL,
  output WriteRF,
  output [2:0] RFInput,
  output Unsigned,
  output [1:0] RFSelector,
  output [1:0] BC_SEL
);

  wire AluSel0, AluSel1, AluSel2, AluSel3, or_1_out;

  or or_1 (or_1_out, div, divu);
  or or_2 (AluSel0, sub, sltu, or_1_out, \xor , \or );
  or or_3 (AluSel1, mulu, mul, div, \nor , \xor );
  or or_4 (AluSel2, \nor , \xor , \or , \and );
  or or_5 (AluSel3, slt, sltu);
  assign ALU_SEL = {4{EN}} & {AluSel3, AluSel2, AluSel1, AluSel0};  // AND_Gate and_1, 4 bits wide
  and and_2 (WritePC, EN, 1'b1);
  or or_6 (Unsigned, mulu, divu);
  assign RFSelector = 2'b10 & {2{EN}};  // AND_Gate and_3, 2 bits wide
  and and_4 (BC_SEL[1], jr, EN);
  and and_5 (WriteRF, ~jr, ~mul, ~mulu, ~div, ~divu, EN);  // AND_Gate

  assign BC_SEL[0] = 1'b0;
  assign RFInput = {mfhi, mflo, mfhi};
endmodule

module I_Mapper (
  input  EN,
  input  addi,
  input  andi,
  input  ori,
  input  xori,
  input  slti,
  input  sltiu,
  output WritePC,
  output WriteRF,
  output ALUA,
  output [1:0] ALUB,
  output [2:0] RF_INPUT,
  output [1:0] RF_SEL,
  output [1:0] BC_SEL,
  output [3:0] ALU_SEL
);

  wire AluSel0, AluSel2, AluSel3;

  or or_1 (AluSel0, ori, xori, sltiu);
  or or_2 (AluSel2, andi, ori, xori);
  or or_3 (AluSel3, slti, sltiu);
  and and_1 (WritePC, EN, 1'b1);
  and and_2 (WriteRF, EN, 1'b1);
  or or_4 (ALUB[0], addi, slti, sltiu);
  or or_5 (ALUB[1], andi, ori, xori);
  assign ALU_SEL = {4{EN}} & {AluSel3, AluSel2, xori, AluSel0};  // AND_Gate and_3, 4 bits wide

  assign ALUA = 1'b0;
  assign BC_SEL = 2'b00;
  assign RF_INPUT = 3'b000;
  assign RF_SEL = 2'b00;

  // Other names for the same wires on the sheet: AluSel1 = xori
endmodule

module Branch_Mapper (
  input  beq,
  input  bne,
  input  blez,
  input  bgtz,
  input  bltz,
  output [2:0] Flag_Sel
);

  or or_1 (Flag_Sel[0], blez, bltz);
  or or_2 (Flag_Sel[1], bgtz, bltz);

  assign Flag_Sel[2] = bne;
endmodule
