// Logisim project s-mips.circ as structural Verilog
module S_MIPS_Board (
  input  DESHABILITAR_DISPATCHER,
  output halt
);

  wire button_1_out, CLK, CS, d_ff_1_q, LCLR, LoadRAM, LoadRAMOn, LW, R_R_W, R_W, ram_dispatcher_1_finished,
       RCS, Reset_out, RST, TTY_EN;
  wire [2:0] KDB;
  wire [3:0] LMask, Mask, ram_1_read_time, ram_1_write_time, RMask;
  wire [6:0] KDB_DATA, TTY_DATA;
  wire [15:0] Addr, LAddr, RAddr;
  wire [31:0] I0, I1, I2, I3, LData, ram_1_data_out_0, ram_1_data_out_1, ram_1_data_out_2, ram_1_data_out_3,
       RI0, RI1, RI2, RI3;

  TTY #(.rows(25), .cols(80)) tty_1 (.data(TTY_DATA), .clk(CLK), .we(TTY_EN), .clr(RST));
  not not_1 (LoadRAMOn, ram_dispatcher_1_finished);
  RAM_Dispatcher ram_dispatcher_1 (
    .WriteTime(ram_1_write_time), .Clock(CLK), .Data(LData), .Address(LAddr), .Mask(LMask),
    .Finished(ram_dispatcher_1_finished), .Write(LW), .CLR(LCLR));
  Keyboard #(.buflen(64)) keyboard_1 (.clk(CLK), .re(KDB[0]), .avail(KDB[2]), .data(KDB_DATA));  // open: clr
  RAM ram_1 (
    .Address(RAddr), .Data_Out_0(ram_1_data_out_0), .Data_Out_1(ram_1_data_out_1),
    .Data_Out_2(ram_1_data_out_2), .Data_Out_3(ram_1_data_out_3), .Data_In_0(RI0), .Data_In_1(RI1),
    .Data_In_2(RI2), .Data_In_3(RI3), .Mask(RMask), .nRead_Write(R_R_W), .Chip_Select(RCS),
    .Read_Time(ram_1_read_time), .Reset(button_1_out), .Write_Time(ram_1_write_time));
  Button button_1 (.out(button_1_out));
  D_Flip_Flop d_ff_1 (.clk(CLK), .D(1'b1), .Q(d_ff_1_q), .reset(Reset_out));  // open: Qn, preset, en
  Button Reset (.out(Reset_out));
  S_MIPS s_mips_1 (
    .Kbd_Enable(KDB[0]), .Address(Addr), .Kbd_Clear(KDB[1]), .Kbd_Available(KDB[2]), .RAM_In_0(I0),
    .Kbd_ASCII_Data(KDB_DATA), .RAM_In_1(I1), .TTY_Enable(TTY_EN), .RAM_In_2(I2), .RAM_In_3(I3),
    .TTY_ASCII_Data(TTY_DATA), .Reset(RST), .RAM_Out_0(ram_1_data_out_0), .Clock(CLK),
    .RAM_Out_1(ram_1_data_out_1), .Stop(halt), .RAM_Out_2(ram_1_data_out_2), .RAM_Out_3(ram_1_data_out_3),
    .Mask(Mask), .Read_Time(ram_1_read_time), .Write_Time(ram_1_write_time), .nRead_Write(R_W),
    .Chip_Select(CS));
  D_Flip_Flop d_ff_2 (.clk(CLK), .D(d_ff_1_q), .Qn(LCLR), .reset(Reset_out));  // open: Q, preset, en
  or or_1 (RST, LCLR, LoadRAM);
  Clock clock_1 (.out(CLK));
  Multiplexer #(.width(32), .enable("false")) multiplexer_1 (.in0(I0), .in1(LData), .out(RI0), .sel(LoadRAM));
  Multiplexer #(.width(32), .enable("false")) multiplexer_2 (.in0(I1), .in1(LData), .out(RI1), .sel(LoadRAM));
  Multiplexer #(.width(32), .enable("false")) multiplexer_3 (.in0(I2), .in1(LData), .out(RI2), .sel(LoadRAM));
  Multiplexer #(.width(32), .enable("false")) multiplexer_4 (.in0(I3), .in1(LData), .out(RI3), .sel(LoadRAM));
  and and_1 (LoadRAM, ~DESHABILITAR_DISPATCHER, LoadRAMOn);  // AND_Gate
  Multiplexer #(.width(16), .enable("false")) multiplexer_5 (.in0(Addr), .in1(LAddr), .out(RAddr), .sel(LoadRAM));
  Multiplexer #(.width(4), .enable("false")) multiplexer_6 (.in0(Mask), .in1(LMask), .out(RMask), .sel(LoadRAM));
  Multiplexer #(.enable("false")) multiplexer_7 (.in0(CS), .in1(LW), .out(RCS), .sel(LoadRAM));
  Multiplexer #(.enable("false")) multiplexer_8 (.in0(R_W), .in1(LW), .out(R_R_W), .sel(LoadRAM));

  // Notes on the sheet:
  //   NO MODIFICAR
  //   Keyboard
endmodule

module RAM (
  input  [15:0] Address,
  input  [31:0] Data_In_0,
  input  [31:0] Data_In_1,
  input  [31:0] Data_In_2,
  input  [31:0] Data_In_3,
  input  [3:0] Mask,
  input  nRead_Write,
  input  Chip_Select,
  input  Reset,
  output [31:0] Data_Out_0,
  output [31:0] Data_Out_1,
  output [31:0] Data_Out_2,
  output [31:0] Data_Out_3,
  output [3:0] Read_Time,
  output [3:0] Write_Time
);

  wire and_2_out, and_3_out, and_4_out, and_5_out, and_6_out, and_7_out, and_8_out, and_9_out, Changed, CLK,
       comparator_2_eq, comparator_3_eq, comparator_4_eq, comparator_5_eq, comparator_6_eq, Count,
       demultiplexer_3_out0, Idle, Idle_q, Load, Load0, Load1, nand_1_out, or_1_out, or_2_out, or_3_out,
       or_4_out, or_5_out, or_6_out, or_7_out, or_8_out, or_9_out, or_10_out, Proc_q, Update_Mem, Zero_Time;
  wire [3:0] counter_1_q, multiplexer_1_out, subtractor_1_out;
  wire [31:0] register_1_q, register_2_q, register_3_q, register_4_q, register_5_q;

  // Probe on 4'b0011
  // Probe on 4'b0010
  Multiplexer #(.width(4), .enable("false")) multiplexer_1 (
    .in0(4'b0011), .in1(4'b0010), .out(multiplexer_1_out), .sel(nRead_Write));
  or or_1 (or_1_out, Idle, Update_Mem);
  or or_2 (or_2_out, ~Chip_Select, Reset);  // OR_Gate
  Subtractor #(.width(4)) subtractor_1 (.a(multiplexer_1_out), .b(4'b0010), .out(subtractor_1_out));  // open: bin, bout
  D_Flip_Flop u_Idle (.clk(CLK), .D(or_1_out), .Q(Idle_q), .preset(or_2_out));  // open: Qn, en, reset
  Demultiplexer #(.enable("false")) demultiplexer_1 (.out0(Idle), .out1(Load0), .in(Idle_q), .sel(Changed));
  // Probe on counter_1_q
  Counter #(.width(4), .max('hf)) counter_1 (
    .load(Load), .D(subtractor_1_out), .count(Count), .Q(counter_1_q), .clk(CLK), .clr(or_3_out));  // open: carry
  or or_3 (or_3_out, ~Chip_Select, Reset);  // OR_Gate
  Comparator #(.width(4), .mode("unsigned")) comparator_1 (
    .a(4'b0000), .b(counter_1_q), .eq(Zero_Time));  // open: gt, lt
  or or_4 (or_4_out, Count, Load0, Load1);
  Register #(.width(32)) register_1 (.D(Data_In_0), .en(Chip_Select), .Q(register_1_q), .clk(CLK), .clr(or_5_out));
  or or_5 (or_5_out, ~Chip_Select, Reset);  // OR_Gate
  Register #(.width(32)) register_2 (.D(Data_In_1), .en(Chip_Select), .Q(register_2_q), .clk(CLK), .clr(or_6_out));
  or or_6 (or_6_out, ~Chip_Select, Reset);  // OR_Gate
  Register #(.width(32)) register_3 (.D(Data_In_2), .en(Chip_Select), .Q(register_3_q), .clk(CLK), .clr(or_7_out));
  or or_7 (or_7_out, ~Chip_Select, Reset);  // OR_Gate
  Register #(.width(32)) register_4 (.D(Data_In_3), .en(Chip_Select), .Q(register_4_q), .clk(CLK), .clr(or_8_out));
  or or_8 (or_8_out, ~Chip_Select, Reset);  // OR_Gate
  Register #(.width(32)) register_5 (
    .D({{11{1'b1}}, nRead_Write, Mask, Address}), .en(Chip_Select), .Q(register_5_q), .clk(CLK),
    .clr(or_9_out));
  or or_9 (or_9_out, ~Chip_Select, Reset);  // OR_Gate
  D_Flip_Flop Proc (.clk(CLK), .D(or_4_out), .Q(Proc_q), .reset(or_10_out));  // open: Qn, preset, en
  or or_10 (or_10_out, ~Chip_Select, Reset);  // OR_Gate
  Demultiplexer #(.enable("false")) demultiplexer_2 (
    .out0(Count), .out1(Update_Mem), .in(demultiplexer_3_out0), .sel(Zero_Time));
  Demultiplexer #(.enable("false")) demultiplexer_3 (
    .out0(demultiplexer_3_out0), .out1(Load1), .in(Proc_q), .sel(Changed));
  Clock clock_1 (.out(CLK));
  Comparator #(.width(32)) comparator_2 (.a(register_1_q), .b(Data_In_0), .eq(comparator_2_eq));  // open: gt, lt
  Comparator #(.width(32)) comparator_3 (.a(register_2_q), .b(Data_In_1), .eq(comparator_3_eq));  // open: gt, lt
  Comparator #(.width(32)) comparator_4 (.a(register_3_q), .b(Data_In_2), .eq(comparator_4_eq));  // open: gt, lt
  Comparator #(.width(32)) comparator_5 (.a(register_4_q), .b(Data_In_3), .eq(comparator_5_eq));  // open: gt, lt
  Comparator #(.width(32)) comparator_6 (
    .a(register_5_q), .b({{11{1'b1}}, nRead_Write, Mask, Address}), .eq(comparator_6_eq));  // open: gt, lt
  nand nand_1 (nand_1_out, comparator_6_eq, comparator_2_eq, comparator_3_eq, comparator_4_eq, comparator_5_eq);
  and and_1 (Changed, nand_1_out, Chip_Select);
  or or_11 (Load, Count, Load1, Load0);
  and and_2 (and_2_out, Mask[0], Update_Mem, nRead_Write);
  and and_3 (and_3_out, Mask[1], Update_Mem, nRead_Write);
  and and_4 (and_4_out, Mask[2], Update_Mem, nRead_Write);
  and and_5 (and_5_out, Mask[3], Update_Mem, nRead_Write);
  RAM_part #(.addrWidth(16), .dataWidth(32), .bus("separate")) ram_1 (
    .addr(Address), .din(Data_In_0), .data(Data_Out_0), .str(and_2_out), .sel(Chip_Select), .clk(CLK),
    .ld(and_6_out), .clr(Reset));
  and and_6 (and_6_out, ~nRead_Write, Idle);  // AND_Gate
  RAM_part #(.addrWidth(16), .dataWidth(32), .bus("separate")) ram_2 (
    .addr(Address), .din(Data_In_1), .data(Data_Out_1), .str(and_3_out), .sel(Chip_Select), .clk(CLK),
    .ld(and_7_out), .clr(Reset));
  and and_7 (and_7_out, ~nRead_Write, Idle);  // AND_Gate
  RAM_part #(.addrWidth(16), .dataWidth(32), .bus("separate")) ram_3 (
    .addr(Address), .din(Data_In_2), .data(Data_Out_2), .str(and_4_out), .sel(Chip_Select), .clk(CLK),
    .ld(and_8_out), .clr(Reset));
  and and_8 (and_8_out, ~nRead_Write, Idle);  // AND_Gate
  RAM_part #(.addrWidth(16), .dataWidth(32), .bus("separate")) ram_4 (
    .addr(Address), .din(Data_In_3), .data(Data_Out_3), .str(and_5_out), .sel(Chip_Select), .clk(CLK),
    .ld(and_9_out), .clr(Reset));
  and and_9 (and_9_out, ~nRead_Write, Idle);  // AND_Gate

  assign Read_Time = 4'b0011;
  assign Write_Time = 4'b0010;

  // Other names for the same wires on the sheet: M0 = Mask[0]; M1 = Mask[1]; M2 = Mask[2]; M3 = Mask[3];
  //   RW = nRead_Write; CLR = Reset; CS = Chip_Select; Load2 = Count

  // Notes on the sheet:
  //   NO MODIFICAR
  //   excepto quizás los valores RT y WT
  //   BANK0
  //   BANK1
  //   BANK2
  //   BANK3
endmodule

module S_MIPS (
  input  Kbd_Available,
  input  [31:0] RAM_Out_0,
  input  [6:0] Kbd_ASCII_Data,
  input  [31:0] RAM_Out_1,
  input  [31:0] RAM_Out_2,
  input  [31:0] RAM_Out_3,
  input  Reset,
  input  Clock,
  input  [3:0] Read_Time,
  input  [3:0] Write_Time,
  output [15:0] Address,
  output Kbd_Enable,
  output Kbd_Clear,
  output TTY_Enable,
  output [6:0] TTY_ASCII_Data,
  output [31:0] RAM_In_0,
  output [31:0] RAM_In_1,
  output Stop,
  output [31:0] RAM_In_2,
  output [31:0] RAM_In_3,
  output [3:0] Mask,
  output nRead_Write,
  output Chip_Select
);

  wire control_unit_1_alua, control_unit_1_dout_sel, control_unit_1_out_7, control_unit_1_unsigned,
       control_unit_1_writepc, control_unit_1_writerf, CSIn, DIn_SEL, END_CS, flag, Ram_RW_in;
  wire [1:0] control_unit_1_alub, control_unit_1_bcselector, control_unit_1_rf_sel, MA_SEL, offst;
  wire [2:0] control_unit_1_flagselector, control_unit_1_rfinput;
  wire [3:0] control_unit_1_alu_sel;
  wire [5:0] funcCode, opCode;
  wire [31:0] DtataPath_Out, endianflip_1_output, n1_bit_32_bit_multiplexer_1_out,
       n1_bit_32_bit_multiplexer_2_out, n2_bit_32_bit_multiplexer_1_output, RAM_Output;

  Data_Path_2 data_path_1 (
    .in_1(n1_bit_32_bit_multiplexer_2_out), .in_2(Clock), .in_3(Reset), .in_4(control_unit_1_writepc),
    .in_5(control_unit_1_alu_sel), .in_6(control_unit_1_bcselector), .in_7(control_unit_1_rf_sel),
    .in_8(control_unit_1_writerf), .in_9(control_unit_1_alua), .in_10(control_unit_1_alub),
    .in_11(control_unit_1_out_7), .in_12(control_unit_1_unsigned), .in_13(control_unit_1_flagselector),
    .in_14(MA_SEL), .in_15(control_unit_1_dout_sel), .in_16(control_unit_1_rfinput), .out_17(opCode),
    .out_18(funcCode), .Flag(flag), .TTY(TTY_ASCII_Data), .Data_Out(DtataPath_Out), .Mask(Mask),
    .Offset(offst), .Address(Address));
  _1_bit_32_bit_Multiplexer u_1_bit_32_bit_multiplexer_1 (
    .i0({32{1'b1}}), .i1({{25{1'b0}}, Kbd_ASCII_Data}), .out(n1_bit_32_bit_multiplexer_1_out),
    .Selector(Kbd_Available));
  _1_bit_32_bit_Multiplexer u_1_bit_32_bit_multiplexer_2 (
    .i0(RAM_Output), .i1(n1_bit_32_bit_multiplexer_1_out), .out(n1_bit_32_bit_multiplexer_2_out),
    .Selector(DIn_SEL));
  RamRW ramrw_1 (
    .Read_Time(Read_Time), .Write_Time(Write_Time), .in_3(Clock), .in_4(Reset), .RWselect(Ram_RW_in),
    .CSIN(CSIn), .END(END_CS), .CS(Chip_Select), .RW(nRead_Write));
  EndianFlip endianflip_1 (.Input(DtataPath_Out), .Output(endianflip_1_output));
  _2_sbit_32_dbit_Demux u_2_sbit_32_dbit_demux_1 (
    .i(endianflip_1_output), .S(offst), .o0(RAM_In_0), .o1(RAM_In_1), .o2(RAM_In_2), .o3(RAM_In_3));
  Control_Unit_2 control_unit_1 (
    .END_CS_IN(END_CS), .RST(Reset), .CLK(Clock), .Func_Code(funcCode), .OP_Code(opCode), .Flag(flag),
    .ALUB(control_unit_1_alub), .out_7(control_unit_1_out_7), .CS(CSIn), .TTY_ENABLE(TTY_Enable),
    .ALU_SEL(control_unit_1_alu_sel), .ALUA(control_unit_1_alua), .RFInput(control_unit_1_rfinput),
    .RF_SEL(control_unit_1_rf_sel), .BCSelector(control_unit_1_bcselector),
    .FlagSelector(control_unit_1_flagselector), .writeRF(control_unit_1_writerf),
    .writePC(control_unit_1_writepc), .\unsigned (control_unit_1_unsigned), .MA_SEL(MA_SEL),
    .DOut_SEL(control_unit_1_dout_sel), .RAM_RW(Ram_RW_in), .DIn_SEL(DIn_SEL), .KBD_EN(Kbd_Enable),
    .halt(Stop));
  _2_bit_32_bit_Multiplexer u_2_bit_32_bit_multiplexer_1 (
    .in_1(RAM_Out_0), .in_2(RAM_Out_1), .in_3(RAM_Out_2), .in_4(RAM_Out_3),
    .Output(n2_bit_32_bit_multiplexer_1_output), .Selector(offst));
  EndianFlip endianflip_2 (.Input(n2_bit_32_bit_multiplexer_1_output), .Output(RAM_Output));

  assign Kbd_Clear = Reset;

  // Other names for the same wires on the sheet: KBD_DATA[6:0] = Kbd_ASCII_Data; CLK = Clock; CS = Chip_Select;
  //   KBD_AVAIL = Kbd_Available; CLR = Reset; KBD_CLR = Reset; RAM_A[15:0] = Address; RAM_INPUT_0[31:0] = RAM_In_0;
  //   RAM_INPUT_1[31:0] = RAM_In_1; RAM_INPUT_2[31:0] = RAM_In_2; RAM_INPUT_3[31:0] = RAM_In_3; RAM_MASK[3:0] = Mask;
  //   RAM_OUTPUT_0[31:0] = RAM_Out_0; RAM_OUTPUT_1[31:0] = RAM_Out_1; RAM_OUTPUT_2[31:0] = RAM_Out_2;
  //   RAM_OUTPUT_3[31:0] = RAM_Out_3; RW = nRead_Write; TTY_DATA[6:0] = TTY_ASCII_Data

  // Notes on the sheet:
  //   SEQUENCING
  //   RAM ADDRESS
  //   DATA FROM RAM
  //   RAM TIMING
  //   RAM CONTROL
  //   KEYBOARD
  //   TTY
  //   DATA TO RAM
  //   DATA WRITE MASK
endmodule

module RAM_Dispatcher (
  input  [3:0] WriteTime,
  input  Clock,
  input  CLR,
  output [31:0] Data,
  output [15:0] Address,
  output [3:0] Mask,
  output Finished,
  output Write
);

  wire demultiplexer_2_out1, demultiplexer_3_out1, End, IDLE_q, IncAddr, Load, or_1_out, or_2_out, While_q,
       WriteEnd;
  wire [3:0] counter_1_q;
  wire [31:0] CurrentAddress_q;

  Counter #(.width(32), .max('hffffffff)) CurrentAddress (
    .count(IncAddr), .Q({CurrentAddress_q[31:18], Address, CurrentAddress_q[1:0]}), .clk(Clock), .clr(CLR));  // open: load, D, carry
  or or_1 (or_1_out, IncAddr, demultiplexer_3_out1, Finished);
  D_Flip_Flop IDLE (.clk(Clock), .D(or_1_out), .Q(IDLE_q), .preset(CLR));  // open: Qn, en, reset
  Demultiplexer #(.enable("false")) demultiplexer_1 (.out0(Load), .out1(Finished), .in(IDLE_q), .sel(End));
  D_Flip_Flop While (.clk(Clock), .D(or_2_out), .Q(While_q), .reset(CLR));  // open: Qn, preset, en
  or or_2 (or_2_out, Write, Load);
  RAM_part #(.addrWidth(18), .dataWidth(32)) ram_1 (
    .addr({Address, CurrentAddress_q[1:0]}), .data(Data), .clk(Clock));  // open: sel, ld, clr
  Demultiplexer #(.enable("false")) demultiplexer_2 (
    .out0(Write), .out1(demultiplexer_2_out1), .in(While_q), .sel(WriteEnd));
  Decoder #(.select(2)) decoder_1 (
    .out0(Mask[0]), .out1(Mask[1]), .out2(Mask[2]), .out3(Mask[3]), .sel(CurrentAddress_q[1:0]));  // open: en
  Demultiplexer #(.enable("false")) demultiplexer_3 (
    .out0(IncAddr), .out1(demultiplexer_3_out1), .in(demultiplexer_2_out1), .sel(End));
  Counter #(.width(4), .max('hf)) counter_1 (
    .load(Load), .D(WriteTime), .count(Write), .Q(counter_1_q), .clk(Clock));  // open: carry, clr
  Comparator #(.width(32)) comparator_1 (.a(Data), .b({32{1'b1}}), .eq(End));  // open: gt, lt
  Comparator #(.width(4)) comparator_2 (.a(4'b0000), .b(counter_1_q), .eq(WriteEnd));  // open: gt, lt

  // Other names for the same wires on the sheet: CLK = Clock; Count = Write; WT[3:0] = WriteTime
endmodule

module EndianFlip (
  input  [31:0] Input,
  output [31:0] Output
);


  assign Output = {Input[7:0], Input[15:8], Input[23:16], Input[31:24]};
endmodule

module RamRW (
  input  [3:0] Read_Time,
  input  [3:0] Write_Time,
  input  in_3,
  input  in_4,
  input  RWselect,
  input  CSIN,
  output END,
  output CS,
  output RW
);

  wire comparator_1_gt, comparator_2_gt, CountRT, demultiplexer_1_out0, demultiplexer_1_out1,
       demultiplexer_2_out0, demultiplexer_2_out1, demultiplexer_3_out0, demultiplexer_3_out1, end_t,
       not_3_out, not_4_out, or_2_out, or_3_out, RST, RTcontinue, WTcontinue;
  wire [3:0] counter_1_q, counter_2_q;

  Comparator #(.width(4)) comparator_1 (.a(Read_Time), .b(counter_1_q), .gt(comparator_1_gt));  // open: eq, lt
  Counter #(.width(4), .max('hf)) counter_1 (
    .count(CountRT), .Q(counter_1_q), .clk(in_3), .clr(RST));  // open: load, D, carry
  Comparator #(.width(4)) comparator_2 (.a(Write_Time), .b(counter_2_q), .gt(comparator_2_gt));  // open: eq, lt
  Counter #(.width(4), .max('hf)) counter_2 (
    .count(RW), .Q(counter_2_q), .clk(in_3), .clr(RST));  // open: load, D, carry
  not not_1 (RTcontinue, comparator_1_gt);
  not not_2 (WTcontinue, comparator_2_gt);
  or or_1 (RST, in_4, end_t);
  Demultiplexer #(.enable("false")) demultiplexer_1 (
    .out0(demultiplexer_1_out0), .out1(demultiplexer_1_out1), .in(CSIN), .sel(RWselect));
  or or_2 (or_2_out, demultiplexer_1_out0, CountRT);
  or or_3 (or_3_out, demultiplexer_1_out1, RW);
  not not_3 (not_3_out, RTcontinue);
  Demultiplexer #(.enable("false")) demultiplexer_2 (
    .out0(demultiplexer_2_out0), .out1(demultiplexer_2_out1), .in(or_2_out), .sel(not_3_out));
  not not_4 (not_4_out, WTcontinue);
  Demultiplexer #(.enable("false")) demultiplexer_3 (
    .out0(demultiplexer_3_out0), .out1(demultiplexer_3_out1), .in(or_3_out), .sel(not_4_out));
  D_Flip_Flop \wait  (.clk(in_3), .D(demultiplexer_2_out1), .Q(CountRT), .reset(RST));  // open: Qn, preset, en
  D_Flip_Flop wait_2 (.clk(in_3), .D(demultiplexer_3_out1), .Q(RW), .reset(RST));  // open: Qn, preset, en
  or or_4 (END, demultiplexer_2_out0, demultiplexer_3_out0);
  D_Flip_Flop wait_3 (.clk(in_3), .D(END), .Q(end_t), .reset(RST));  // open: Qn, preset, en
  or or_5 (CS, CountRT, RW);

  // Other names for the same wires on the sheet: Clk = in_3; CS0 = CountRT; CountWT = RW; CS1 = RW; clear = in_4;
  //   reset = in_4; RT[3:0] = Read_Time; select = RWselect; WT[3:0] = Write_Time
endmodule

module Data_Path_2 (
  input  [31:0] in_1,
  input  in_2,
  input  in_3,
  input  in_4,
  input  [3:0] in_5,
  input  [1:0] in_6,
  input  [1:0] in_7,
  input  in_8,
  input  in_9,
  input  [1:0] in_10,
  input  in_11,
  input  in_12,
  input  [2:0] in_13,
  input  [1:0] in_14,
  input  in_15,
  input  [2:0] in_16,
  output [5:0] out_17,
  output [5:0] out_18,
  output Flag,
  output [6:0] TTY,
  output [31:0] Data_Out,
  output [3:0] Mask,
  output [1:0] Offset,
  output [15:0] Address
);

  wire eq, gtz, hi_lo, letz, ltz, neq;
  wire [4:0] n2_sbit_5_dbit_multiplexer_1_output, Rd, Rs, Rt;
  wire [15:0] \const ;
  wire [25:0] destino;
  wire [31:0] _0__const, ALUOut, bc_1_pc, HI, LO, n1_bit_32_bit_multiplexer_1_out,
       n2_bit_32_bit_multiplexer_1_output, n2_bit_32_bit_multiplexer_2_output,
       n3_bit_32_bit_multiplexer_1_output, OutHI, OutLO, PC, random, RT_t, S__const, SP;
  wire [31:7] RS_t;

  _2_sbit_5_dbit_Multiplexer u_2_sbit_5_dbit_multiplexer_1 (
    .in_1({5{1'b1}}), .in_2(Rt), .in_3(Rd), .Output(n2_sbit_5_dbit_multiplexer_1_output), .Selector(in_7));  // open: in_4
  // Probe on in_7
  _3_bit_32_bit_Multiplexer u_3_bit_32_bit_multiplexer_1 (
    .in_1(ALUOut), .in_2(in_1), .in_5(random), .in_6(OutHI), .in_7(OutLO),
    .Output(n3_bit_32_bit_multiplexer_1_output), .in_9(in_16));  // open: in_3, in_4, in_8
  // Probe on in_16
  BC bc_1 (.in_1(PC), .in_2({RS_t, TTY}), .in_3(\const ), .in_4(destino), .in_5(in_6), .PC(bc_1_pc));
  // Probe on n2_sbit_5_dbit_multiplexer_1_output
  // Probe on Rt
  // Probe on Rs
  // Probe on PC
  Register #(.width(32)) register_1 (.D(bc_1_pc), .en(in_4), .Q(PC), .clk(in_2), .clr(in_3));
  _32x32_RF u_32x32_rf_1 (
    .DA(n2_sbit_5_dbit_multiplexer_1_output), .DI(n3_bit_32_bit_multiplexer_1_output), .R_W(in_8), .SA(Rs),
    .SB(Rt), .Clk(in_2), .Reset(in_3), .A({RS_t, TTY}), .B(RT_t), .Hi(HI), .Lo(LO), .mul_div(hi_lo),
    .out_13(OutHI), .out_15(OutLO), .SP(SP));
  // Probe on S__const
  assign S__const = {{16{\const [15]}}, \const };  // Bit_Extender bit_extender_1
  assign _0__const = {{16{1'b0}}, \const };  // Bit_Extender bit_extender_2
  Random #(.width(32)) random_1 (.clk(in_2), .out(random));  // open: next, clr
  // Probe on in_10
  ALU_2 alu_1 (
    .in_1(n1_bit_32_bit_multiplexer_1_out), .in_2(in_12), .in_3(in_5),
    .in_4(n2_bit_32_bit_multiplexer_1_output), .out_6(HI), .out_8(ALUOut), .out_10(LO), .out_5(neq),
    .out_7(eq), .Mul_Div(hi_lo), .out_11(letz), .out_12(gtz), .out_13(ltz));
  _1_bit_32_bit_Multiplexer u_1_bit_32_bit_multiplexer_1 (
    .i0({RS_t, TTY}), .i1(SP), .out(n1_bit_32_bit_multiplexer_1_out), .Selector(in_9));
  _2_bit_32_bit_Multiplexer u_2_bit_32_bit_multiplexer_1 (
    .in_1(RT_t), .in_2(S__const), .in_3(_0__const), .in_4(32'h4),
    .Output(n2_bit_32_bit_multiplexer_1_output), .Selector(in_10));
  ID id_1 (
    .in_1(in_11), .in_2(in_2), .in_3(in_1), .out_4(out_17), .out_5(Rs), .out_6(Rt), .out_7(Rd),
    .out_8(out_18), .out_9(\const ), .out_10(destino));
  // Probe on ALUOut
  _2_bit_32_bit_Multiplexer u_2_bit_32_bit_multiplexer_2 (
    .in_1(PC), .in_2(ALUOut), .in_3(SP),
    .Output({n2_bit_32_bit_multiplexer_2_output[31:20], Address, Offset, n2_bit_32_bit_multiplexer_2_output[1:0]}),
    .Selector(in_14));  // open: in_4
  // Probe on in_13
  // Probe on TTY
  _1_bit_32_bit_Multiplexer u_1_bit_32_bit_multiplexer_2 (
    .i0({RS_t, TTY}), .i1(RT_t), .out(Data_Out), .Selector(in_15));
  Decoder #(.select(2), .enable("false")) decoder_1 (
    .out0(Mask[0]), .out1(Mask[1]), .out2(Mask[2]), .out3(Mask[3]), .sel(Offset));
  _3_bit_Multiplexer u_3_bit_multiplexer_1 (
    .in_1(eq), .in_2(letz), .in_3(gtz), .in_4(ltz), .in_5(neq), .Output(Flag), .in_9(in_13));  // open: in_6, in_7, in_8

  // Other names for the same wires on the sheet: ALUA = in_9; ALUB[1:0] = in_10; ALUselect[3:0] = in_5;
  //   BCselect[1:0] = in_6; Clk = in_2; DataIn[31:0] = in_1; DOS = in_15; flagSel[2:0] = in_13; func[5:0] = out_18;
  //   LoadPC = in_4; MAS[1:0] = in_14; opcode[5:0] = out_17; reset = in_3; RFInSelect[2:0] = in_16;
  //   RFselect[1:0] = in_7; RS_t[6:0] = TTY; unsigned = in_12; writeID = in_11; writeRF = in_8
endmodule

module ID (
  input  in_1,
  input  in_2,
  input  [31:0] in_3,
  output [5:0] out_4,
  output [4:0] out_5,
  output [4:0] out_6,
  output [4:0] out_7,
  output [5:0] out_8,
  output [15:0] out_9,
  output [25:0] out_10
);

  Register #(.width(32)) register_1 (
    .D(in_3), .en(in_1), .Q({out_4, out_5, out_6, out_7, out_9[10:6], out_8}), .clk(in_2));  // open: clr

  assign {out_9[15:11], out_9[5:0]} = {out_7, out_8};
  assign out_10 = {out_5, out_6, out_7, out_9[10:6], out_8};

  // Other names for the same wires on the sheet: const[15:0] = {out_7, out_9[10:6], out_8};
  //   destino[25:0] = {out_5, out_6, out_7, out_9[10:6], out_8}; func[5:0] = out_8; Rd[4:0] = out_7; Rt[4:0] = out_6;
  //   Rs[4:0] = out_5; opcode[5:0] = out_4; CLK = in_2; enable = in_1
endmodule

module BC (
  input  [31:0] in_1,
  input  [31:0] in_2,
  input  [15:0] in_3,
  input  [25:0] in_4,
  input  [1:0] in_5,
  output [31:0] PC
);

  wire [31:0] _4_offset32, offset32, PC__4, PC__4_4_offset32;

  Adder #(.width(32)) adder_1 (.a(in_1), .b(32'h4), .out(PC__4));  // open: cin, cout
  Shifter #(.width(32)) shifter_1 (.in(offset32), .\dist (5'b00010), .out(_4_offset32));
  assign offset32 = {{16{in_3[15]}}, in_3};  // Bit_Extender bit_extender_1
  Adder #(.width(32)) adder_2 (.a(PC__4), .b(_4_offset32), .out(PC__4_4_offset32));  // open: cin, cout
  Multiplexer #(.select(2), .width(32), .enable("false")) multiplexer_1 (
    .in0(PC__4), .in1(PC__4_4_offset32), .in2(in_2), .in3({in_1[31:28], in_4, 2'b00}), .out(PC), .sel(in_5));
  // Probe on in_5

  // Other names for the same wires on the sheet: dest[31:2] = {in_1[31:28], in_4}; destino[25:0] = in_4;
  //   PC_t[31:0] = in_1; offset[15:0] = in_3; RS[31:0] = in_2; select[1:0] = in_5
endmodule

module ALU_2 (
  input  [31:0] in_1,
  input  in_2,
  input  [3:0] in_3,
  input  [31:0] in_4,
  output out_5,
  output [31:0] out_6,
  output out_7,
  output [31:0] out_8,
  output Mul_Div,
  output [31:0] out_10,
  output out_11,
  output out_12,
  output out_13
);

  wire [0:0] lt, ltu;
  wire [31:0] add, \and , C, multHI, multLO, \nor , \or , R, sub, \xor ;

  assign \and  = in_1 & in_4;  // AND_Gate and_1, 32 bits wide
  assign \or  = in_1 | in_4;  // OR_Gate or_1, 32 bits wide
  assign \xor  = in_1 ^ in_4;  // XOR_Gate xor_1, 32 bits wide
  Comparator #(.width(32), .mode("unsigned")) comparator_1 (.a(in_1), .b(in_4), .eq(out_7), .lt(ltu[0]));  // open: gt
  Mult mult_1 (.in_1(in_1), .in_2(in_4), .in_3(in_2), .out_4(multHI), .out_5(multLO));
  assign \nor  = ~(in_1 | in_4);  // NOR_Gate nor_1, 32 bits wide
  Multiplexer #(.width(32), .enable("false")) multiplexer_1 (.in0(multHI), .in1(R), .out(out_6), .sel(in_3[0]));
  Multiplexer #(.width(32), .enable("false")) multiplexer_2 (.in0(multLO), .in1(C), .out(out_10), .sel(in_3[0]));
  Div div_1 (.in_1(in_1), .in_2(in_4), .in_3(in_2), .Cocient(C), .Remainder(R));
  Adder #(.width(32)) adder_1 (.a(in_1), .b(in_4), .out(add));  // open: cin, cout
  Subtractor #(.width(32)) subtractor_1 (.a(in_1), .b(in_4), .out(sub));  // open: bin, bout
  Comparator #(.width(32)) comparator_2 (.a(in_1), .b(in_4), .eq(out_7), .lt(lt[0]));  // open: gt
  not not_1 (out_11, out_12);
  Comparator #(.width(32)) comparator_3 (.a(in_1), .b({32{1'b0}}), .gt(out_12), .lt(out_13));  // open: eq
  Multiplexer #(.select(4), .width(32), .enable("false")) multiplexer_3 (
    .in0(add), .in1(sub), .in4(\and ), .in5(\or ), .in6(\nor ), .in7(\xor ), .in8({{31{1'b0}}, lt[0]}),
    .in9({{31{1'b0}}, ltu[0]}), .out(out_8), .sel(in_3));  // open: in2, in3, in10, in11, in12, in13, in14, in15
  // Probe on in_1
  // Probe on in_4
  not not_2 (out_5, out_7);
  and and_2 (Mul_Div, in_3[1], ~in_3[2], ~in_3[3]);  // AND_Gate
  // Probe on out_6
  // Probe on R
  // Probe on out_10

  // Other names for the same wires on the sheet: A[31:0] = in_1; B[31:0] = in_4; equ = out_7; gtz = out_12;
  //   HI[31:0] = out_6; letz = out_11; LO[31:0] = out_10; ltz = out_13; RES[31:0] = out_8; select[3:0] = in_3;
  //   unsigned = in_2

  // Notes on the sheet:
  //   Logic
  //   Operators
  //   ALU
  //   Aritmetic
  //   Outputs
  //   Flags
endmodule

module AbsVal (
  input  [31:0] in_1,
  input  in_2,
  output [31:0] out_3,
  output out_4
);

  wire bitselector_1_out;
  wire [31:0] negator_1_out;

  Negator #(.width(32)) negator_1 (.in(in_1), .out(negator_1_out));
  and and_1 (out_4, ~in_2, bitselector_1_out);  // AND_Gate
  BitSelector #(.width(32)) bitselector_1 (.in(in_1), .out(bitselector_1_out), .sel({5{1'b1}}));
  Multiplexer #(.width(32)) multiplexer_1 (.in0(in_1), .in1(negator_1_out), .out(out_3), .sel(out_4));  // open: en

  // Other names for the same wires on the sheet: Input[31:0] = in_1

  // Notes on the sheet:
  //   ABSOLUTE VALUE
endmodule

module Mult (
  input  [31:0] in_1,
  input  [31:0] in_2,
  input  in_3,
  output [31:0] out_4,
  output [31:0] out_5
);

  wire adder_1_cout, sign, signA, signB, xor_1_out;
  wire [31:0] absA, absB, absHI, absLO, bit_extender_1_out, not_1_out, not_2_out, sHI, sLO;

  AbsVal absval_1 (.in_1(in_1), .out_3(absA), .out_4(signA), .in_2(in_3));
  AbsVal absval_2 (.in_1(in_2), .out_3(absB), .out_4(signB), .in_2(in_3));
  xor xor_1 (xor_1_out, signA, signB);
  and and_1 (sign, xor_1_out, ~in_3);  // AND_Gate
  assign not_1_out = ~absLO;  // NOT_Gate not_1, 32 bits wide
  assign not_2_out = ~absHI;  // NOT_Gate not_2, 32 bits wide
  Multiplier #(.width(32)) multiplier_1 (.a(absA), .b(absB), .out(absLO), .cout(absHI));  // open: cin
  Adder #(.width(32)) adder_1 (.a(not_1_out), .b(32'h1), .out(sLO), .cout(adder_1_cout));  // open: cin
  assign bit_extender_1_out = {{31{1'b0}}, adder_1_cout};  // Bit_Extender bit_extender_1
  Adder #(.width(32)) adder_2 (.a(bit_extender_1_out), .b(not_2_out), .out(sHI));  // open: cin, cout
  Multiplexer #(.width(32), .enable("false")) multiplexer_1 (.in0(absHI), .in1(sHI), .out(out_4), .sel(sign));
  Multiplexer #(.width(32), .enable("false")) multiplexer_2 (.in0(absLO), .in1(sLO), .out(out_5), .sel(sign));

  // Other names for the same wires on the sheet: A[31:0] = in_1; B[31:0] = in_2; HI[31:0] = out_4; LO[31:0] = out_5;
  //   unsigned = in_3

  // Notes on the sheet:
  //   MULTIPLIER
  //   UNSIGNED-SIGNED
endmodule

module Div (
  input  [31:0] in_1,
  input  [31:0] in_2,
  input  in_3,
  output [31:0] Cocient,
  output [31:0] Remainder
);

  wire and_1_out, and_2_out, sign, xor_1_out;
  wire [31:0] C, multiplexer_1_out, multiplexer_2_out, negator_1_out, negator_2_out, negator_3_out;

  xor xor_1 (xor_1_out, in_1[31], in_2[31]);
  Negator #(.width(32)) negator_1 (.in(in_1), .out(negator_1_out));
  and and_1 (and_1_out, in_1[31], ~in_3);  // AND_Gate
  and and_2 (and_2_out, ~in_3, in_2[31]);  // AND_Gate
  Negator #(.width(32)) negator_2 (.in(in_2), .out(negator_2_out));
  and and_3 (sign, xor_1_out, ~in_3);  // AND_Gate
  Multiplexer #(.width(32), .enable("false")) multiplexer_1 (
    .in0(in_1), .in1(negator_1_out), .out(multiplexer_1_out), .sel(and_1_out));
  Multiplexer #(.width(32), .enable("false")) multiplexer_2 (
    .in0(in_2), .in1(negator_2_out), .out(multiplexer_2_out), .sel(and_2_out));
  Divider #(.width(32)) divider_1 (
    .a(multiplexer_1_out), .b(multiplexer_2_out), .out(C), .rem(Remainder));  // open: upper
  Negator #(.width(32)) negator_3 (.in(C), .out(negator_3_out));
  Multiplexer #(.width(32), .enable("false")) multiplexer_3 (.in0(C), .in1(negator_3_out), .out(Cocient), .sel(sign));

  // Other names for the same wires on the sheet: A[31:0] = in_1; signA = in_1[31]; B[31:0] = in_2; signB = in_2[31];
  //   R[31:0] = Remainder; unsigned = in_3

  // Notes on the sheet:
  //   DIVIDER
  //   (UNSIGNED-SIGNED)
endmodule

module _32_bit_Register (
  input  CLK,
  input  RST,
  input  Load,
  input  [31:0] Data_In,
  output [31:0] out_5
);

  wire undriven, undriven_2, undriven_3, undriven_4, undriven_5, undriven_6, undriven_7, undriven_8,
       undriven_9, undriven_10, undriven_11, undriven_12, undriven_13, undriven_14, undriven_15, undriven_16,
       undriven_17, undriven_18, undriven_19, undriven_20, undriven_21, undriven_22, undriven_23,
       undriven_24, undriven_25, undriven_26, undriven_27, undriven_28, undriven_29, undriven_30,
       undriven_31, undriven_32;

  D_Flip_Flop d_ff_1 (.clk(CLK), .D(Data_In[0]), .Q(out_5[0]), .preset(undriven), .en(Load), .reset(RST));  // open: Qn
  D_Flip_Flop d_ff_2 (
    .clk(CLK), .D(Data_In[1]), .Q(out_5[1]), .preset(undriven_2), .en(Load), .reset(RST));  // open: Qn
  D_Flip_Flop d_ff_3 (
    .clk(CLK), .D(Data_In[2]), .Q(out_5[2]), .preset(undriven_3), .en(Load), .reset(RST));  // open: Qn
  D_Flip_Flop d_ff_4 (
    .clk(CLK), .D(Data_In[3]), .Q(out_5[3]), .preset(undriven_4), .en(Load), .reset(RST));  // open: Qn
  D_Flip_Flop d_ff_5 (
    .clk(CLK), .D(Data_In[4]), .Q(out_5[4]), .preset(undriven_5), .en(Load), .reset(RST));  // open: Qn
  D_Flip_Flop d_ff_6 (
    .clk(CLK), .D(Data_In[5]), .Q(out_5[5]), .preset(undriven_6), .en(Load), .reset(RST));  // open: Qn
  D_Flip_Flop d_ff_7 (
    .clk(CLK), .D(Data_In[6]), .Q(out_5[6]), .preset(undriven_7), .en(Load), .reset(RST));  // open: Qn
  D_Flip_Flop d_ff_8 (
    .clk(CLK), .D(Data_In[7]), .Q(out_5[7]), .preset(undriven_8), .en(Load), .reset(RST));  // open: Qn
  D_Flip_Flop d_ff_9 (
    .clk(CLK), .D(Data_In[8]), .Q(out_5[8]), .preset(undriven_9), .en(Load), .reset(RST));  // open: Qn
  D_Flip_Flop d_ff_10 (
    .clk(CLK), .D(Data_In[9]), .Q(out_5[9]), .preset(undriven_10), .en(Load), .reset(RST));  // open: Qn
  D_Flip_Flop d_ff_11 (
    .clk(CLK), .D(Data_In[10]), .Q(out_5[10]), .preset(undriven_11), .en(Load), .reset(RST));  // open: Qn
  D_Flip_Flop d_ff_12 (
    .clk(CLK), .D(Data_In[11]), .Q(out_5[11]), .preset(undriven_12), .en(Load), .reset(RST));  // open: Qn
  D_Flip_Flop d_ff_13 (
    .clk(CLK), .D(Data_In[12]), .Q(out_5[12]), .preset(undriven_13), .en(Load), .reset(RST));  // open: Qn
  D_Flip_Flop d_ff_14 (
    .clk(CLK), .D(Data_In[13]), .Q(out_5[13]), .preset(undriven_14), .en(Load), .reset(RST));  // open: Qn
  D_Flip_Flop d_ff_15 (
    .clk(CLK), .D(Data_In[14]), .Q(out_5[14]), .preset(undriven_15), .en(Load), .reset(RST));  // open: Qn
  D_Flip_Flop d_ff_16 (
    .clk(CLK), .D(Data_In[15]), .Q(out_5[15]), .preset(undriven_16), .en(Load), .reset(RST));  // open: Qn
  D_Flip_Flop d_ff_17 (
    .clk(CLK), .D(Data_In[16]), .Q(out_5[16]), .preset(undriven_17), .en(Load), .reset(RST));  // open: Qn
  D_Flip_Flop d_ff_18 (
    .clk(CLK), .D(Data_In[17]), .Q(out_5[17]), .preset(undriven_18), .en(Load), .reset(RST));  // open: Qn
  D_Flip_Flop d_ff_19 (
    .clk(CLK), .D(Data_In[18]), .Q(out_5[18]), .preset(undriven_19), .en(Load), .reset(RST));  // open: Qn
  D_Flip_Flop d_ff_20 (
    .clk(CLK), .D(Data_In[19]), .Q(out_5[19]), .preset(undriven_20), .en(Load), .reset(RST));  // open: Qn
  D_Flip_Flop d_ff_21 (
    .clk(CLK), .D(Data_In[20]), .Q(out_5[20]), .preset(undriven_21), .en(Load), .reset(RST));  // open: Qn
  D_Flip_Flop d_ff_22 (
    .clk(CLK), .D(Data_In[21]), .Q(out_5[21]), .preset(undriven_22), .en(Load), .reset(RST));  // open: Qn
  D_Flip_Flop d_ff_23 (
    .clk(CLK), .D(Data_In[22]), .Q(out_5[22]), .preset(undriven_23), .en(Load), .reset(RST));  // open: Qn
  D_Flip_Flop d_ff_24 (
    .clk(CLK), .D(Data_In[23]), .Q(out_5[23]), .preset(undriven_24), .en(Load), .reset(RST));  // open: Qn
  D_Flip_Flop d_ff_25 (
    .clk(CLK), .D(Data_In[24]), .Q(out_5[24]), .preset(undriven_25), .en(Load), .reset(RST));  // open: Qn
  D_Flip_Flop d_ff_26 (
    .clk(CLK), .D(Data_In[25]), .Q(out_5[25]), .preset(undriven_26), .en(Load), .reset(RST));  // open: Qn
  D_Flip_Flop d_ff_27 (
    .clk(CLK), .D(Data_In[26]), .Q(out_5[26]), .preset(undriven_27), .en(Load), .reset(RST));  // open: Qn
  D_Flip_Flop d_ff_28 (
    .clk(CLK), .D(Data_In[27]), .Q(out_5[27]), .preset(undriven_28), .en(Load), .reset(RST));  // open: Qn
  D_Flip_Flop d_ff_29 (
    .clk(CLK), .D(Data_In[28]), .Q(out_5[28]), .preset(undriven_29), .en(Load), .reset(RST));  // open: Qn
  D_Flip_Flop d_ff_30 (
    .clk(CLK), .D(Data_In[29]), .Q(out_5[29]), .preset(undriven_30), .en(Load), .reset(RST));  // open: Qn
  D_Flip_Flop d_ff_31 (
    .clk(CLK), .D(Data_In[30]), .Q(out_5[30]), .preset(undriven_31), .en(Load), .reset(RST));  // open: Qn
  D_Flip_Flop d_ff_32 (
    .clk(CLK), .D(Data_In[31]), .Q(out_5[31]), .preset(undriven_32), .en(Load), .reset(RST));  // open: Qn

  // Other names for the same wires on the sheet: i0[7:0] = Data_In[7:0]; i1[7:0] = Data_In[15:8];
  //   i2[7:0] = Data_In[23:16]; i3[7:0] = Data_In[31:24]; en = Load; o0[7:0] = out_5[7:0]; o1[7:0] = out_5[15:8];
  //   o2[7:0] = out_5[23:16]; o3[7:0] = out_5[31:24]
endmodule

module _32x32_RF (
  input  [4:0] DA,
  input  [31:0] DI,
  input  R_W,
  input  [4:0] SA,
  input  [4:0] SB,
  input  Clk,
  input  Reset,
  input  [31:0] Hi,
  input  [31:0] Lo,
  input  mul_div,
  output [31:0] A,
  output [31:0] B,
  output [31:0] out_13,
  output [31:0] SP,
  output [31:0] out_15
);

  wire i0, i1, i2, i3, i4, i5, i6, i7, i8, i9, i10, i11, i12, i13, i14, i15, i16, i17, i18, i19, i20, i21,
       i22, i23, i24, i25, i26, i27, i28, i29, i30, i31;
  wire [31:0] o0, o1, o2, o3, o4, o5, o6, o7, o8, o9, o10, o11, o12, o13, o14, o15, o16, o17, o18, o19, o20,
       o21, o22, o23, o24, o25, o26, o27, o28, o29, o30;

  Demultiplexer #(.select(5)) demultiplexer_1 (
    .out0(i0), .out1(i1), .out2(i2), .out3(i3), .out4(i4), .out5(i5), .out6(i6), .out7(i7), .out8(i8),
    .out9(i9), .out10(i10), .out11(i11), .out12(i12), .out13(i13), .out14(i14), .out15(i15), .out16(i16),
    .out17(i17), .out18(i18), .out19(i19), .out20(i20), .out21(i21), .out22(i22), .out23(i23), .out24(i24),
    .out25(i25), .out26(i26), .out27(i27), .out28(i28), .out29(i29), .out30(i30), .out31(i31), .in(R_W),
    .sel(DA));  // open: en
  // Probe on o26
  _32_bit_Register u_32_bit_register_1 (.CLK(Clk), .RST(Reset), .Load(i0), .Data_In(DI), .out_5(o0));
  _32_bit_Register u_32_bit_register_2 (.CLK(Clk), .RST(Reset), .Load(i1), .Data_In(DI), .out_5(o1));
  _32_bit_Register u_32_bit_register_3 (.CLK(Clk), .RST(Reset), .Load(i2), .Data_In(DI), .out_5(o2));
  _32_bit_Register u_32_bit_register_4 (.CLK(Clk), .RST(Reset), .Load(i3), .Data_In(DI), .out_5(o3));
  _32_bit_Register u_32_bit_register_5 (.CLK(Clk), .RST(Reset), .Load(i4), .Data_In(DI), .out_5(o4));
  _32_bit_Register u_32_bit_register_6 (.CLK(Clk), .RST(Reset), .Load(i5), .Data_In(DI), .out_5(o5));
  _32_bit_Register u_32_bit_register_7 (.CLK(Clk), .RST(Reset), .Load(i6), .Data_In(DI), .out_5(o6));
  _32_bit_Register u_32_bit_register_8 (.CLK(Clk), .RST(Reset), .Load(i7), .Data_In(DI), .out_5(o7));
  // Probe on o27
  _32_bit_Register u_32_bit_register_9 (.CLK(Clk), .RST(Reset), .Load(i8), .Data_In(DI), .out_5(o8));
  _32_bit_Register u_32_bit_register_10 (.CLK(Clk), .RST(Reset), .Load(i9), .Data_In(DI), .out_5(o9));
  _32_bit_Register u_32_bit_register_11 (.CLK(Clk), .RST(Reset), .Load(i10), .Data_In(DI), .out_5(o10));
  _32_bit_Register u_32_bit_register_12 (.CLK(Clk), .RST(Reset), .Load(i11), .Data_In(DI), .out_5(o11));
  _32_bit_Register u_32_bit_register_13 (.CLK(Clk), .RST(Reset), .Load(i12), .Data_In(DI), .out_5(o12));
  _32_bit_Register u_32_bit_register_14 (.CLK(Clk), .RST(Reset), .Load(i13), .Data_In(DI), .out_5(o13));
  _32_bit_Register u_32_bit_register_15 (.CLK(Clk), .RST(Reset), .Load(i14), .Data_In(DI), .out_5(o14));
  _32_bit_Register u_32_bit_register_16 (.CLK(Clk), .RST(Reset), .Load(i15), .Data_In(DI), .out_5(o15));
  _32_bit_Register u_32_bit_register_17 (.CLK(Clk), .RST(Reset), .Load(mul_div), .Data_In(Hi), .out_5(out_13));
  // Probe on o8
  // Probe on o0
  _32_bit_Register u_32_bit_register_18 (.CLK(Clk), .RST(Reset), .Load(i16), .Data_In(DI), .out_5(o16));
  _32_bit_Register u_32_bit_register_19 (.CLK(Clk), .RST(Reset), .Load(i17), .Data_In(DI), .out_5(o17));
  _32_bit_Register u_32_bit_register_20 (.CLK(Clk), .RST(Reset), .Load(i18), .Data_In(DI), .out_5(o18));
  _32_bit_Register u_32_bit_register_21 (.CLK(Clk), .RST(Reset), .Load(i19), .Data_In(DI), .out_5(o19));
  _32_bit_Register u_32_bit_register_22 (.CLK(Clk), .RST(Reset), .Load(i20), .Data_In(DI), .out_5(o20));
  _32_bit_Register u_32_bit_register_23 (.CLK(Clk), .RST(Reset), .Load(i21), .Data_In(DI), .out_5(o21));
  _32_bit_Register u_32_bit_register_24 (.CLK(Clk), .RST(Reset), .Load(i22), .Data_In(DI), .out_5(o22));
  _32_bit_Register u_32_bit_register_25 (.CLK(Clk), .RST(Reset), .Load(i23), .Data_In(DI), .out_5(o23));
  _32_bit_Register u_32_bit_register_26 (.CLK(Clk), .RST(Reset), .Load(mul_div), .Data_In(Lo), .out_5(out_15));
  // Probe on o29
  _32_bit_Register u_32_bit_register_27 (.CLK(Clk), .RST(Reset), .Load(i24), .Data_In(DI), .out_5(o24));
  _32_bit_Register u_32_bit_register_28 (.CLK(Clk), .RST(Reset), .Load(i25), .Data_In(DI), .out_5(o25));
  _32_bit_Register u_32_bit_register_29 (.CLK(Clk), .RST(Reset), .Load(i26), .Data_In(DI), .out_5(o26));
  _32_bit_Register u_32_bit_register_30 (.CLK(Clk), .RST(Reset), .Load(i27), .Data_In(DI), .out_5(o27));
  _32_bit_Register u_32_bit_register_31 (.CLK(Clk), .RST(Reset), .Load(i28), .Data_In(DI), .out_5(o28));
  _32_bit_Register u_32_bit_register_32 (.CLK(Clk), .RST(Reset), .Load(i29), .Data_In(DI), .out_5(o29));
  _32_bit_Register u_32_bit_register_33 (.CLK(Clk), .RST(Reset), .Load(i30), .Data_In(DI), .out_5(o30));
  _32_bit_Register u_32_bit_register_34 (.CLK(Clk), .RST(Reset), .Load(i31), .Data_In(DI), .out_5(SP));
  // Probe on o28
  _5_bit_32_bit_Multiplexer u_5_bit_32_bit_multiplexer_1 (
    .in_1(o0), .in_2(o1), .in_3(o2), .in_4(o3), .in_5(o4), .in_6(o5), .in_7(o6), .in_8(o7), .in_9(o8),
    .in_10(o9), .in_11(o10), .in_12(o11), .in_13(o12), .in_14(o13), .in_15(o14), .in_16(o15), .in_17(o16),
    .in_18(o17), .in_19(o18), .in_20(o19), .in_21(o20), .in_22(o21), .in_23(o22), .in_24(o23), .in_25(o24),
    .in_26(o25), .in_27(o26), .in_28(o27), .in_29(o28), .in_30(o29), .in_31(o30), .in_32(SP), .in_33(SA),
    .Output(A));
  _5_bit_32_bit_Multiplexer u_5_bit_32_bit_multiplexer_2 (
    .in_1(o0), .in_2(o1), .in_3(o2), .in_4(o3), .in_5(o4), .in_6(o5), .in_7(o6), .in_8(o7), .in_9(o8),
    .in_10(o9), .in_11(o10), .in_12(o11), .in_13(o12), .in_14(o13), .in_15(o14), .in_16(o15), .in_17(o16),
    .in_18(o17), .in_19(o18), .in_20(o19), .in_21(o20), .in_22(o21), .in_23(o22), .in_24(o23), .in_25(o24),
    .in_26(o25), .in_27(o26), .in_28(o27), .in_29(o28), .in_30(o29), .in_31(o30), .in_32(SP), .in_33(SB),
    .Output(B));

  // Other names for the same wires on the sheet: _0 = Reset; o31[31:0] = SP; OutHi[31:0] = out_13;
  //   OutLo[31:0] = out_15; W = R_W

  // Notes on the sheet:
  //   Inputs
  //   Data Address
  //   Data In
  //   Read/Write
  //   Selector A
  //   Selector B
  //   0 Const
  //   R31 - SP
  //   Outputs
  //   Data A
  //   Data B
endmodule

module Control_Unit_2 (
  input  END_CS_IN,
  input  RST,
  input  CLK,
  input  [5:0] Func_Code,
  input  [5:0] OP_Code,
  input  Flag,
  output out_7,
  output CS,
  output TTY_ENABLE,
  output [3:0] ALU_SEL,
  output [1:0] ALUB,
  output ALUA,
  output [2:0] RFInput,
  output [1:0] RF_SEL,
  output [1:0] BCSelector,
  output [2:0] FlagSelector,
  output writeRF,
  output writePC,
  output \unsigned ,
  output [1:0] MA_SEL,
  output DOut_SEL,
  output RAM_RW,
  output DIn_SEL,
  output KBD_EN,
  output halt
);

  wire _1_Cycle_q, add, addi, ALUA_pop, ALUA_SEL_Imm, ALUA_stack, \and , andi, beq, bgtz, blez, bltz, bne,
       branch, BranchEnd, CS_EN_Instruction, CS_EN_pop, CS_EN_push, CS_EN_stack, demultiplexer_1_out0,
       demultiplexer_1_out1, demultiplexer_2_out1, div, divu, halt_t, IDLE_q, immediate, ImmEnd, jmp, jmpEnd,
       jr, load_Word, LoadEnd, mfhi, mflo, mul, mulu, n1_bit_demultiplexer_1_o1, n1_bit_demultiplexer_2_o0,
       n1_bit_demultiplexer_3_o1, n1_bit_demultiplexer_4_o0, n1_bit_demultiplexer_5_o0,
       n1_bit_demultiplexer_5_o1, n1_bit_demultiplexer_6_o0, n1_bit_demultiplexer_6_o1,
       n1_bit_demultiplexer_9_o1, next, nop, \nor , not_1_out, not_2_out, not_3_out, not_4_out, not_5_out,
       \or , or_1_out, or_2_out, or_4_out, or_5_out, or_7_out, or_10_out, or_11_out, or_17_out, ori,
       push_tty, rnd, slt, slti, sltiu, sltu, special, SpecialEnd, stack, StackEnd, stBranch, stImm,
       stLoad_Word, store_Word, StoreEnd, stSpecial, stStack, stStore_Word, stZero, sub, WAIT_READ_2_q,
       WAIT_READ_q, WRITE_RF_Imm, WRITE_RF_Zero, WritePC_Imm, WritePC_stack, WritePC_Store, WritePC_Zero,
       WRTE_RF_stack, \xor , xori, zero, ZeroEnd;
  wire [0:0] ALU_SEL_push, ALUB_SEL_Load, BC_SEL_Branch, RF_Input_pop, RF_SEL_Load;
  wire [1:0] ALUB_SEL_Imm, ALUB_stack, BC_SEL_Imm, BC_SEL_Zero, MA_SEL_stack, RF_SEL_Imm, RF_SEL_Zero;
  wire [1:1] BC_SEL_Jmp, RF_SEL_rnd_kbd;
  wire [2:0] RF_Input_Imm, RF_Input_Zero;
  wire [2:2] RF_Input_rnd;
  wire [3:0] ALU_SEL_Imm, ALU_SEL_Zero;

  _1_bit_Demultiplexer u_1_bit_demultiplexer_1 (
    .i(or_1_out), .S(not_1_out), .o0(WritePC_Store), .o1(n1_bit_demultiplexer_1_o1));
  or or_1 (or_1_out, stStore_Word, DOut_SEL);
  _1_bit_Demultiplexer u_1_bit_demultiplexer_2 (
    .i(stStack), .S(push_tty), .o0(n1_bit_demultiplexer_2_o0), .o1(ALU_SEL_push[0]));
  Op_Code_Decoder op_code_decoder_1 (
    .o0(OP_Code[0]), .o1(OP_Code[1]), .o2(OP_Code[2]), .o3(OP_Code[3]), .o4(OP_Code[4]), .o5(OP_Code[5]),
    .ENABLE(1'b1), .zero(zero), .beq(beq), .stack(stack), .addi(addi), .bne(bne), .special(special),
    .andi(andi), .blez(blez), .ori(ori), .bgtz(bgtz), .xori(xori), .bltz(bltz), .slti(slti), .lw(load_Word),
    .sltiu(sltiu), .sw(store_Word), .jump(jmp));
  Func_Code_Decoder func_code_decoder_1 (
    .f0(Func_Code[0]), .f1(Func_Code[1]), .f2(Func_Code[2]), .f3(Func_Code[3]), .f4(Func_Code[4]),
    .f5(Func_Code[5]), .EN(1'b1), .nop_pop(nop), .add(add), .\and (\and ), .push_tty(push_tty), .sub(sub),
    .\or (\or ), .halt(halt_t), .mul(mul), .\nor (\nor ), .rnd(rnd), .mulu(mulu), .\xor (\xor ), .div(div),
    .mfhi(mfhi), .mflo(mflo), .divu(divu), .slt(slt), .jr(jr), .sltu(sltu));  // open: kbd
  Branch_Mapper branch_mapper_1 (.beq(beq), .bne(bne), .blez(blez), .bgtz(bgtz), .bltz(bltz), .Flag_Sel(FlagSelector));
  not not_1 (not_1_out, END_CS_IN);
  or or_2 (or_2_out, n1_bit_demultiplexer_2_o0, CS_EN_pop);
  _1_bit_Demultiplexer u_1_bit_demultiplexer_3 (
    .i(or_2_out), .S(not_2_out), .o0(RF_Input_pop[0]), .o1(n1_bit_demultiplexer_3_o1));
  not not_2 (not_2_out, END_CS_IN);
  _1_bit_Demultiplexer u_1_bit_demultiplexer_4 (
    .i(stBranch), .S(Flag), .o0(n1_bit_demultiplexer_4_o0), .o1(BC_SEL_Branch[0]));
  D_Flip_Flop WAIT (.clk(CLK), .D(n1_bit_demultiplexer_1_o1), .Q(DOut_SEL), .reset(RST));  // open: Qn, preset, en
  D_Flip_Flop _1_Cycle (.clk(CLK), .D(ALU_SEL_push[0]), .Q(_1_Cycle_q), .reset(RST));  // open: Qn, preset, en
  D_Flip_Flop IDLE (.clk(CLK), .D(demultiplexer_1_out1), .Q(IDLE_q), .preset(RST));  // open: Qn, en, reset
  Demultiplexer demultiplexer_1 (
    .out0(demultiplexer_1_out0), .out1(demultiplexer_1_out1), .in(IDLE_q), .sel(RST));  // open: en
  or or_3 (branch, beq, bne, blez, bgtz, bltz);
  D_Flip_Flop _1_Cycle_2 (.clk(CLK), .D(WritePC_Store), .Q(StoreEnd), .reset(RST));  // open: Qn, preset, en
  D_Flip_Flop WAIT_2 (.clk(CLK), .D(n1_bit_demultiplexer_3_o1), .Q(CS_EN_pop), .reset(RST));  // open: Qn, preset, en
  or or_4 (or_4_out, _1_Cycle_q, CS_EN_push);
  _1_bit_Demultiplexer u_1_bit_demultiplexer_5 (
    .i(or_4_out), .S(not_3_out), .o0(n1_bit_demultiplexer_5_o0), .o1(n1_bit_demultiplexer_5_o1));
  not not_3 (not_3_out, END_CS_IN);
  or or_5 (or_5_out, n1_bit_demultiplexer_4_o0, BC_SEL_Branch[0]);
  D_Flip_Flop WAIT_3 (.clk(CLK), .D(n1_bit_demultiplexer_5_o1), .Q(CS_EN_push), .reset(RST));  // open: Qn, preset, en
  or or_6 (CS_EN_Instruction, next, demultiplexer_1_out0);
  D_Flip_Flop _1_CYCLE_3 (.clk(CLK), .D(or_5_out), .Q(BranchEnd), .reset(RST));  // open: Qn, preset, en
  D_Flip_Flop _1_Cycle_4 (.clk(CLK), .D(RF_Input_pop[0]), .Q(ALUA_pop), .reset(RST));  // open: Qn, preset, en
  Demultiplexer demultiplexer_2 (
    .out0(out_7), .out1(demultiplexer_2_out1), .in(or_7_out), .sel(not_4_out));  // open: en
  or or_7 (or_7_out, CS_EN_Instruction, WAIT_READ_q);
  not not_4 (not_4_out, END_CS_IN);
  or or_8 (immediate, addi, andi, ori, xori, slti, sltiu);
  _1_bit_Demultiplexer u_1_bit_demultiplexer_6 (
    .i(stSpecial), .S(halt_t), .o0(n1_bit_demultiplexer_6_o0), .o1(n1_bit_demultiplexer_6_o1));
  or or_9 (WritePC_stack, ALUA_pop, n1_bit_demultiplexer_5_o0);
  _1_bit_Demultiplexer u_1_bit_demultiplexer_7 (
    .i(n1_bit_demultiplexer_6_o0), .S(push_tty), .o0(RF_SEL_rnd_kbd[1]), .o1(TTY_ENABLE));
  or or_10 (or_10_out, n1_bit_demultiplexer_6_o1, halt);
  D_Flip_Flop _1_Cycle_5 (.clk(CLK), .D(WritePC_stack), .Q(StackEnd), .reset(RST));  // open: Qn, preset, en
  D_Flip_Flop WAIT_READ (.clk(CLK), .D(demultiplexer_2_out1), .Q(WAIT_READ_q), .reset(RST));  // open: Qn, preset, en
  D_Flip_Flop _1_CYCLE_6 (.clk(CLK), .D(stZero), .Q(ZeroEnd), .reset(RST));  // open: Qn, preset, en
  Zero_Mapper zero_mapper_1 (
    .EN(stZero), .add(add), .sub(sub), .mul(mul), .mulu(mulu), .div(div), .divu(divu), .\and (\and ),
    .\or (\or ), .\nor (\nor ), .\xor (\xor ), .mfhi(mfhi), .mflo(mflo), .jr(jr), .slt(slt), .sltu(sltu),
    .WritePC(WritePC_Zero), .ALU_SEL(ALU_SEL_Zero), .WriteRF(WRITE_RF_Zero), .RFInput(RF_Input_Zero),
    .Unsigned(\unsigned ), .RFSelector(RF_SEL_Zero), .BC_SEL(BC_SEL_Zero), .nop(nop));
  D_Flip_Flop _1_CYCLE_7 (.clk(CLK), .D(stImm), .Q(ImmEnd), .reset(RST));  // open: Qn, preset, en
  I_Mapper i_mapper_1 (
    .EN(stImm), .addi(addi), .andi(andi), .ori(ori), .xori(xori), .slti(slti), .sltiu(sltiu),
    .WritePC(WritePC_Imm), .WriteRF(WRITE_RF_Imm), .ALUA(ALUA_SEL_Imm), .ALUB(ALUB_SEL_Imm),
    .RF_INPUT(RF_Input_Imm), .RF_SEL(RF_SEL_Imm), .BC_SEL(BC_SEL_Imm), .ALU_SEL(ALU_SEL_Imm));
  _1_bit_Demultiplexer u_1_bit_demultiplexer_8 (.i(RF_SEL_rnd_kbd[1]), .S(rnd), .o0(DIn_SEL), .o1(RF_Input_rnd[2]));
  D_Flip_Flop u_Halt (.clk(CLK), .D(or_10_out), .Q(halt), .reset(RST));  // open: Qn, preset, en
  D_Flip_Flop WAIT_READ_2 (.clk(CLK), .D(out_7), .Q(WAIT_READ_2_q), .reset(RST));  // open: Qn, preset, en
  _1_bit_Demultiplexer u_1_bit_demultiplexer_9 (
    .i(or_11_out), .S(not_5_out), .o0(RF_SEL_Load[0]), .o1(n1_bit_demultiplexer_9_o1));
  or or_11 (or_11_out, stLoad_Word, ALUB_SEL_Load[0]);
  not not_5 (not_5_out, END_CS_IN);
  or or_12 (ALUA_stack, ALUA_pop, ALU_SEL_push[0]);
  and and_1 (stZero, WAIT_READ_2_q, zero);
  and and_2 (stImm, WAIT_READ_2_q, immediate);
  and and_3 (stBranch, WAIT_READ_2_q, branch);
  and and_4 (stLoad_Word, WAIT_READ_2_q, load_Word);
  and and_5 (stStore_Word, WAIT_READ_2_q, store_Word);
  D_Flip_Flop WAIT_4 (
    .clk(CLK), .D(n1_bit_demultiplexer_9_o1), .Q(ALUB_SEL_Load[0]), .reset(RST));  // open: Qn, preset, en
  assign ALUB_stack = {2{ALUA_pop}} | {2{ALU_SEL_push[0]}};  // OR_Gate or_13, 2 bits wide
  or or_14 (WRTE_RF_stack, RF_Input_pop[0], ALUA_pop, ALU_SEL_push[0]);
  or or_15 (CS_EN_stack, CS_EN_push, CS_EN_pop);
  assign MA_SEL_stack = {CS_EN_pop, 1'b0} | {CS_EN_push, 1'b0};  // OR_Gate or_16, 2 bits wide
  D_Flip_Flop _1_CYCLE_8 (.clk(CLK), .D(BC_SEL_Jmp[1]), .Q(jmpEnd), .reset(RST));  // open: Qn, preset, en
  D_Flip_Flop _1_Cycle_9 (.clk(CLK), .D(RF_SEL_Load[0]), .Q(LoadEnd), .reset(RST));  // open: Qn, preset, en
  or or_17 (or_17_out, DIn_SEL, RF_Input_rnd[2], TTY_ENABLE);
  and and_6 (stSpecial, WAIT_READ_2_q, special);
  and and_7 (stStack, WAIT_READ_2_q, stack);
  and and_8 (BC_SEL_Jmp[1], WAIT_READ_2_q, jmp);
  or or_18 (next, jmpEnd, ZeroEnd, ImmEnd, BranchEnd, LoadEnd, StoreEnd, SpecialEnd, StackEnd);
  D_Flip_Flop _1_Cycle_10 (.clk(CLK), .D(or_17_out), .Q(SpecialEnd), .reset(RST));  // open: Qn, preset, en
  assign ALU_SEL = ALU_SEL_Zero | ALU_SEL_Imm | {3'b000, ALU_SEL_push[0]};  // OR_Gate or_19, 4 bits wide
  or or_20 (CS, CS_EN_Instruction, ALUB_SEL_Load[0], DOut_SEL, CS_EN_stack);
  assign ALUB = ALUB_SEL_Imm | ALUB_stack | {1'b0, DOut_SEL} | {1'b0, ALUB_SEL_Load[0]};  // OR_Gate or_21, 2 bits wide
  or or_22 (ALUA, ALUA_SEL_Imm, ALUA_stack);
  assign RFInput = RF_Input_Zero | RF_Input_Imm | {2'b00, RF_SEL_Load[0]} | {2'b00, DIn_SEL} | {RF_Input_rnd[2], 2'b00} | {2'b00, RF_Input_pop[0]};  // OR_Gate or_23, 3 bits wide
  assign RF_SEL = RF_SEL_Zero | RF_SEL_Imm | {RF_Input_pop[0], 1'b0} | {1'b0, RF_SEL_Load[0]} | {RF_SEL_rnd_kbd[1], 1'b0};  // OR_Gate or_24, 2 bits wide
  assign BCSelector = BC_SEL_Zero | BC_SEL_Imm | {1'b0, BC_SEL_Branch[0]} | {2{BC_SEL_Jmp[1]}};  // OR_Gate or_25, 2 bits wide
  or or_26 (writeRF, WRITE_RF_Zero, WRITE_RF_Imm, RF_SEL_Load[0], RF_SEL_rnd_kbd[1], WRTE_RF_stack);
  or or_27 (writePC, WritePC_Zero, WritePC_Imm, stBranch, RF_SEL_Load[0], BC_SEL_Jmp[1], WritePC_Store, RF_SEL_rnd_kbd[1], TTY_ENABLE, WritePC_stack);
  assign MA_SEL = {1'b0, DOut_SEL} | {1'b0, ALUB_SEL_Load[0]} | MA_SEL_stack;  // OR_Gate or_28, 2 bits wide
  or or_29 (RAM_RW, DOut_SEL, CS_EN_push);

  assign KBD_EN = DIn_SEL;

  // Other names for the same wires on the sheet: ALU_SEL_stack[0] = ALU_SEL_push[0]; ALUA_push = ALU_SEL_push[0];
  //   ALUB_push[1:0] = {2{ALU_SEL_push[0]}}; WRITE_RF_push0 = ALU_SEL_push[0]; ALUB_pop[1:0] = {2{ALUA_pop}};
  //   WRITE_RF_pop1 = ALUA_pop; BC_SEL_Jmp[0] = BC_SEL_Jmp[1]; stJmp = BC_SEL_Jmp[1]; WritePC_Jmp = BC_SEL_Jmp[1];
  //   Flag_SEL[2:0] = FlagSelector; haltOut = halt; CS_EN_Load = ALUB_SEL_Load[0]; MA_SEL_Load[0] = ALUB_SEL_Load[0];
  //   MA_SEL_pop[1] = CS_EN_pop; MA_SEL_push[1] = CS_EN_push; RAM_RW_push = CS_EN_push; RAM_RW_stack = CS_EN_push;
  //   ALUB_SEL_Store[0] = DOut_SEL; CS_EN_Store = DOut_SEL; DOut_SEL_Store = DOut_SEL; MA_SEL_Store[0] = DOut_SEL;
  //   RAM_RW_store = DOut_SEL; DIn_SEL_kbd = DIn_SEL; RF_Input_kbd[0] = DIn_SEL; WRITE_RF_rnd_kbd = RF_SEL_rnd_kbd[1];
  //   WritePC_rnd_kbd = RF_SEL_rnd_kbd[1]; RF_Input_stack[0] = RF_Input_pop[0]; RF_SEL_pop[1] = RF_Input_pop[0];
  //   RF_SEL_stack[1] = RF_Input_pop[0]; WRITE_RF_pop0 = RF_Input_pop[0]; RFInput_Load[0] = RF_SEL_Load[0];
  //   WRITE_RF_Load = RF_SEL_Load[0]; WritePC_Load = RF_SEL_Load[0]; WritePC_Branch = stBranch; Write_ID = out_7;
  //   TTY_EN = TTY_ENABLE; WritePC_TTY = TTY_ENABLE

  // Notes on the sheet:
  //   kbd
endmodule

module Op_Code_Decoder (
  input  o0,
  input  o1,
  input  o2,
  input  o3,
  input  o4,
  input  o5,
  input  ENABLE,
  output zero,
  output beq,
  output stack,
  output addi,
  output bne,
  output special,
  output andi,
  output blez,
  output jump,
  output ori,
  output bgtz,
  output xori,
  output bltz,
  output slti,
  output lw,
  output sltiu,
  output sw
);

  wire and_1_out, and_2_out, and_3_out, and_4_out, and_5_out, and_6_out, and_7_out, and_15_out, and_16_out,
       and_17_out, and_18_out, and_19_out, and_20_out, and_21_out, and_29_out, and_30_out, and_31_out;

  and and_1 (and_1_out, ~o0, ~o1, ~o2, ~o3, ~o4, ~o5);  // AND_Gate
  and and_2 (and_2_out, ~o0, ~o1, ~o2, o3, ~o4, ~o5);  // AND_Gate
  and and_3 (and_3_out, ~o0, ~o1, o2, o3, ~o4, ~o5);  // AND_Gate
  and and_4 (and_4_out, o0, ~o1, o2, o3, ~o4, ~o5);  // AND_Gate
  and and_5 (and_5_out, ~o0, o1, o2, o3, ~o4, ~o5);  // AND_Gate
  and and_6 (and_6_out, ~o0, o1, ~o2, o3, ~o4, ~o5);  // AND_Gate
  and and_7 (and_7_out, o0, o1, ~o2, o3, ~o4, ~o5);  // AND_Gate
  and and_8 (zero, and_1_out, ENABLE);
  and and_9 (addi, and_2_out, ENABLE);
  and and_10 (andi, and_3_out, ENABLE);
  and and_11 (ori, and_4_out, ENABLE);
  and and_12 (xori, and_5_out, ENABLE);
  and and_13 (slti, and_6_out, ENABLE);
  and and_14 (sltiu, and_7_out, ENABLE);
  and and_15 (and_15_out, ~o0, ~o1, o2, ~o3, ~o4, ~o5);  // AND_Gate
  and and_16 (and_16_out, o0, ~o1, o2, ~o3, ~o4, ~o5);  // AND_Gate
  and and_17 (and_17_out, ~o0, o1, o2, ~o3, ~o4, ~o5);  // AND_Gate
  and and_18 (and_18_out, o0, o1, o2, ~o3, ~o4, ~o5);  // AND_Gate
  and and_19 (and_19_out, o0, ~o1, ~o2, ~o3, ~o4, ~o5);  // AND_Gate
  and and_20 (and_20_out, o0, o1, ~o2, ~o3, ~o4, o5);  // AND_Gate
  and and_21 (and_21_out, o0, o1, ~o2, o3, ~o4, o5);  // AND_Gate
  and and_22 (beq, and_15_out, ENABLE);
  and and_23 (bne, and_16_out, ENABLE);
  and and_24 (blez, and_17_out, ENABLE);
  and and_25 (bgtz, and_18_out, ENABLE);
  and and_26 (bltz, and_19_out, ENABLE);
  and and_27 (lw, and_20_out, ENABLE);
  and and_28 (sw, and_21_out, ENABLE);
  and and_29 (and_29_out, ~o0, ~o1, ~o2, o3, o4, o5);  // AND_Gate
  and and_30 (and_30_out, o0, o1, o2, o3, o4, o5);
  and and_31 (and_31_out, ~o0, o1, ~o2, ~o3, ~o4, ~o5);  // AND_Gate
  and and_32 (stack, and_29_out, ENABLE);
  and and_33 (special, and_30_out, ENABLE);
  and and_34 (jump, and_31_out, ENABLE);

  // Other names for the same wires on the sheet: EN = ENABLE
endmodule

module Func_Code_Decoder (
  input  f0,
  input  f1,
  input  f2,
  input  f3,
  input  f4,
  input  f5,
  input  EN,
  output nop_pop,
  output add,
  output \and ,
  output push_tty,
  output sub,
  output \or ,
  output halt,
  output mul,
  output \nor ,
  output rnd,
  output mulu,
  output \xor ,
  output kbd,
  output div,
  output mfhi,
  output mflo,
  output divu,
  output slt,
  output jr,
  output sltu
);

  wire and_1_out, and_2_out, and_3_out, and_4_out, and_5_out, and_6_out, and_7_out, and_8_out, and_17_out,
       and_18_out, and_19_out, and_20_out, and_21_out, and_22_out, and_23_out, and_31_out, and_32_out,
       and_33_out, and_34_out, and_35_out;

  and and_1 (and_1_out, ~f0, ~f1, ~f2, ~f3, ~f4, f5);  // AND_Gate
  and and_2 (and_2_out, ~f0, f1, ~f2, ~f3, ~f4, f5);  // AND_Gate
  and and_3 (and_3_out, ~f0, ~f1, ~f2, f3, f4, ~f5);  // AND_Gate
  and and_4 (and_4_out, f0, ~f1, ~f2, f3, f4, ~f5);  // AND_Gate
  and and_5 (and_5_out, ~f0, f1, ~f2, f3, f4, ~f5);  // AND_Gate
  and and_6 (and_6_out, f0, f1, ~f2, f3, f4, ~f5);  // AND_Gate
  and and_7 (and_7_out, ~f0, f1, ~f2, f3, ~f4, f5);  // AND_Gate
  and and_8 (and_8_out, f0, f1, ~f2, f3, ~f4, f5);  // AND_Gate
  and and_9 (add, and_1_out, EN);
  and and_10 (sub, and_2_out, EN);
  and and_11 (mul, and_3_out, EN);
  and and_12 (mulu, and_4_out, EN);
  and and_13 (div, and_5_out, EN);
  and and_14 (divu, and_6_out, EN);
  and and_15 (slt, and_7_out, EN);
  and and_16 (sltu, and_8_out, EN);
  and and_17 (and_17_out, ~f0, ~f1, f2, ~f3, ~f4, f5);  // AND_Gate
  and and_18 (and_18_out, f0, ~f1, f2, ~f3, ~f4, f5);  // AND_Gate
  and and_19 (and_19_out, f0, f1, f2, ~f3, ~f4, f5);  // AND_Gate
  and and_20 (and_20_out, ~f0, ~f1, ~f2, f3, ~f4, f5);  // AND_Gate
  and and_21 (and_21_out, ~f0, ~f1, ~f2, ~f3, f4, ~f5);  // AND_Gate
  and and_22 (and_22_out, ~f0, f1, ~f2, ~f3, f4, ~f5);  // AND_Gate
  and and_23 (and_23_out, ~f0, ~f1, ~f2, f3, ~f4, ~f5);  // AND_Gate
  and and_24 (\and , and_17_out, EN);
  and and_25 (\or , and_18_out, EN);
  and and_26 (\nor , and_19_out, EN);
  and and_27 (\xor , and_20_out, EN);
  and and_28 (mfhi, and_21_out, EN);
  and and_29 (mflo, and_22_out, EN);
  and and_30 (jr, and_23_out, EN);
  and and_31 (and_31_out, ~f0, ~f1, ~f2, ~f3, ~f4, ~f5);  // AND_Gate
  and and_32 (and_32_out, f0, ~f1, ~f2, ~f3, ~f4, ~f5);  // AND_Gate
  and and_33 (and_33_out, f0, f1, f2, f3, f4, f5);
  and and_34 (and_34_out, ~f0, f1, ~f2, ~f3, ~f4, ~f5);  // AND_Gate
  and and_35 (and_35_out, ~f0, ~f1, f2, ~f3, ~f4, ~f5);  // AND_Gate
  and and_36 (nop_pop, and_31_out, EN);
  and and_37 (push_tty, and_32_out, EN);
  and and_38 (halt, and_33_out, EN);
  and and_39 (rnd, and_34_out, EN);
  and and_40 (kbd, and_35_out, EN);
endmodule

module Zero_Mapper (
  input  EN,
  input  add,
  input  sub,
  input  mul,
  input  mulu,
  input  div,
  input  divu,
  input  \and ,
  input  \or ,
  input  \nor ,
  input  \xor ,
  input  mfhi,
  input  mflo,
  input  jr,
  input  slt,
  input  sltu,
  input  nop,
  output WritePC,
  output [3:0] ALU_SEL,
  output WriteRF,
  output [2:0] RFInput,
  output Unsigned,
  output [1:0] RFSelector,
  output [1:0] BC_SEL
);

  wire AluSel0, AluSel1, AluSel2, AluSel3, and_3_out, or_1_out, or_6_out;
  wire [2:2] or_7_out;

  or or_1 (or_1_out, div, divu);
  or or_2 (AluSel0, sub, sltu, or_1_out, \xor , \or );
  or or_3 (AluSel1, mulu, mul, or_1_out, \nor , \xor );
  or or_4 (AluSel2, \nor , \xor , \or , \and );
  or or_5 (AluSel3, slt, sltu);
  assign ALU_SEL = {4{EN}} & {AluSel3, AluSel2, AluSel1, AluSel0};  // AND_Gate and_1, 4 bits wide
  and and_2 (WritePC, EN, 1'b1);
  and and_3 (and_3_out, EN, ~nop);  // AND_Gate
  or or_6 (or_6_out, mulu, divu);
  assign RFSelector = 2'b10 & {2{EN}};  // AND_Gate and_4, 2 bits wide
  and and_5 (BC_SEL[1], jr, EN);
  and and_6 (WriteRF, ~jr, ~mul, ~mulu, ~div, ~divu, and_3_out);  // AND_Gate
  or or_7 (or_7_out[2], mfhi, mflo);
  and and_7 (Unsigned, EN, or_6_out);
  assign RFInput = {3{EN}} & {or_7_out[2], mflo, mfhi};  // AND_Gate and_8, 3 bits wide

  assign BC_SEL[0] = 1'b0;
endmodule

module I_Mapper (
  input  EN,
  input  addi,
  input  andi,
  input  ori,
  input  xori,
  input  slti,
  input  sltiu,
  output WritePC,
  output WriteRF,
  output ALUA,
  output [1:0] ALUB,
  output [2:0] RF_INPUT,
  output [1:0] RF_SEL,
  output [1:0] BC_SEL,
  output [3:0] ALU_SEL
);

  wire AluSel0, AluSel2, AluSel3;
  wire [1:0] or_4_out;

  or or_1 (AluSel0, ori, xori, sltiu);
  or or_2 (AluSel2, andi, ori, xori);
  or or_3 (AluSel3, slti, sltiu);
  and and_1 (WritePC, EN, 1'b1);
  and and_2 (WriteRF, EN, 1'b1);
  or or_4 (or_4_out[0], addi, slti, sltiu);
  or or_5 (or_4_out[1], andi, ori, xori);
  assign ALU_SEL = {4{EN}} & {AluSel3, AluSel2, xori, AluSel0};  // AND_Gate and_3, 4 bits wide
  assign ALUB = {2{EN}} & or_4_out;  // AND_Gate and_4, 2 bits wide

  assign ALUA = 1'b0;
  assign BC_SEL = 2'b00;
  assign RF_INPUT = 3'b000;
  assign RF_SEL = {1'b0, EN};

  // Other names for the same wires on the sheet: AluSel1 = xori
endmodule

module Branch_Mapper (
  input  beq,
  input  bne,
  input  blez,
  input  bgtz,
  input  bltz,
  output [2:0] Flag_Sel
);

  or or_1 (Flag_Sel[0], blez, bltz);
  or or_2 (Flag_Sel[1], bgtz, bltz);

  assign Flag_Sel[2] = bne;
endmodule

module _1_bit_Multiplexer (
  input  i0,
  input  i1,
  input  Selector,
  output out
);

  wire and_1_out, and_2_out;

  and and_1 (and_1_out, i0, ~Selector);  // AND_Gate
  and and_2 (and_2_out, i1, Selector);
  or or_1 (out, and_1_out, and_2_out);
endmodule

module _2_bit_Multiplexer (
  input  in_1,
  input  in_2,
  input  in_3,
  input  in_4,
  input  [1:0] Selector,
  output Output
);

  wire n1_bit_multiplexer_1_out, n1_bit_multiplexer_2_out;

  _1_bit_Multiplexer u_1_bit_multiplexer_1 (
    .i0(in_1), .i1(in_2), .out(n1_bit_multiplexer_1_out), .Selector(Selector[0]));
  _1_bit_Multiplexer u_1_bit_multiplexer_2 (
    .i0(in_3), .i1(in_4), .out(n1_bit_multiplexer_2_out), .Selector(Selector[0]));
  _1_bit_Multiplexer u_1_bit_multiplexer_3 (
    .i0(n1_bit_multiplexer_1_out), .i1(n1_bit_multiplexer_2_out), .out(Output), .Selector(Selector[1]));
endmodule

module _3_bit_Multiplexer (
  input  in_1,
  input  in_2,
  input  in_3,
  input  in_4,
  input  in_5,
  input  in_6,
  input  in_7,
  input  in_8,
  input  [2:0] in_9,
  output Output
);

  wire n2_bit_multiplexer_1_output, n2_bit_multiplexer_2_output;

  _2_bit_Multiplexer u_2_bit_multiplexer_1 (
    .in_1(in_1), .in_2(in_2), .in_3(in_3), .in_4(in_4), .Output(n2_bit_multiplexer_1_output),
    .Selector(in_9[1:0]));
  _2_bit_Multiplexer u_2_bit_multiplexer_2 (
    .in_1(in_5), .in_2(in_6), .in_3(in_7), .in_4(in_8), .Output(n2_bit_multiplexer_2_output),
    .Selector(in_9[1:0]));
  _1_bit_Multiplexer u_1_bit_multiplexer_1 (
    .i0(n2_bit_multiplexer_1_output), .i1(n2_bit_multiplexer_2_output), .out(Output), .Selector(in_9[2]));
endmodule

module _4_bit_Multiplexer (
  input  in_1,
  input  in_2,
  input  in_3,
  input  in_4,
  input  in_5,
  input  in_6,
  input  in_7,
  input  in_8,
  input  in_9,
  input  in_10,
  input  in_11,
  input  in_12,
  input  in_13,
  input  in_14,
  input  in_15,
  input  in_16,
  input  [3:0] in_17,
  output Output
);

  wire n3_bit_multiplexer_1_output, n3_bit_multiplexer_2_output;

  _3_bit_Multiplexer u_3_bit_multiplexer_1 (
    .in_1(in_1), .in_2(in_2), .in_3(in_3), .in_4(in_4), .in_5(in_5), .in_6(in_6), .in_7(in_7), .in_8(in_8),
    .Output(n3_bit_multiplexer_1_output), .in_9(in_17[2:0]));
  _3_bit_Multiplexer u_3_bit_multiplexer_2 (
    .in_1(in_9), .in_2(in_10), .in_3(in_11), .in_4(in_12), .in_5(in_13), .in_6(in_14), .in_7(in_15),
    .in_8(in_16), .Output(n3_bit_multiplexer_2_output), .in_9(in_17[2:0]));
  _1_bit_Multiplexer u_1_bit_multiplexer_1 (
    .i0(n3_bit_multiplexer_1_output), .i1(n3_bit_multiplexer_2_output), .out(Output), .Selector(in_17[3]));
endmodule

module _5_bit_Multiplexer (
  input  in_1,
  input  in_2,
  input  in_3,
  input  in_4,
  input  in_5,
  input  in_6,
  input  in_7,
  input  in_8,
  input  in_9,
  input  in_10,
  input  in_11,
  input  in_12,
  input  in_13,
  input  in_14,
  input  in_15,
  input  in_16,
  input  in_17,
  input  in_18,
  input  in_19,
  input  in_20,
  input  in_21,
  input  in_22,
  input  in_23,
  input  in_24,
  input  in_25,
  input  in_26,
  input  in_27,
  input  in_28,
  input  in_29,
  input  in_30,
  input  in_31,
  input  in_32,
  input  [4:0] in_33,
  output Output
);

  wire n2_bit_multiplexer_1_output, n2_bit_multiplexer_2_output, n2_bit_multiplexer_3_output,
       n2_bit_multiplexer_4_output, n2_bit_multiplexer_5_output, n2_bit_multiplexer_6_output,
       n2_bit_multiplexer_7_output, n2_bit_multiplexer_8_output, n2_bit_multiplexer_9_output,
       n2_bit_multiplexer_10_output;

  _2_bit_Multiplexer u_2_bit_multiplexer_1 (
    .in_1(in_1), .in_2(in_2), .in_3(in_3), .in_4(in_4), .Output(n2_bit_multiplexer_1_output),
    .Selector(in_33[1:0]));
  _2_bit_Multiplexer u_2_bit_multiplexer_2 (
    .in_1(in_5), .in_2(in_6), .in_3(in_7), .in_4(in_8), .Output(n2_bit_multiplexer_2_output),
    .Selector(in_33[1:0]));
  _2_bit_Multiplexer u_2_bit_multiplexer_3 (
    .in_1(in_9), .in_2(in_10), .in_3(in_11), .in_4(in_12), .Output(n2_bit_multiplexer_3_output),
    .Selector(in_33[1:0]));
  _2_bit_Multiplexer u_2_bit_multiplexer_4 (
    .in_1(in_13), .in_2(in_14), .in_3(in_15), .in_4(in_16), .Output(n2_bit_multiplexer_4_output),
    .Selector(in_33[1:0]));
  _2_bit_Multiplexer u_2_bit_multiplexer_5 (
    .in_1(in_17), .in_2(in_18), .in_3(in_19), .in_4(in_20), .Output(n2_bit_multiplexer_5_output),
    .Selector(in_33[1:0]));
  _2_bit_Multiplexer u_2_bit_multiplexer_6 (
    .in_1(in_21), .in_2(in_22), .in_3(in_23), .in_4(in_24), .Output(n2_bit_multiplexer_6_output),
    .Selector(in_33[1:0]));
  _2_bit_Multiplexer u_2_bit_multiplexer_7 (
    .in_1(in_25), .in_2(in_26), .in_3(in_27), .in_4(in_28), .Output(n2_bit_multiplexer_7_output),
    .Selector(in_33[1:0]));
  _2_bit_Multiplexer u_2_bit_multiplexer_8 (
    .in_1(in_29), .in_2(in_30), .in_3(in_31), .in_4(in_32), .Output(n2_bit_multiplexer_8_output),
    .Selector(in_33[1:0]));
  _2_bit_Multiplexer u_2_bit_multiplexer_9 (
    .in_1(n2_bit_multiplexer_1_output), .in_2(n2_bit_multiplexer_2_output),
    .in_3(n2_bit_multiplexer_3_output), .in_4(n2_bit_multiplexer_4_output),
    .Output(n2_bit_multiplexer_9_output), .Selector(in_33[3:2]));
  _2_bit_Multiplexer u_2_bit_multiplexer_10 (
    .in_1(n2_bit_multiplexer_5_output), .in_2(n2_bit_multiplexer_6_output),
    .in_3(n2_bit_multiplexer_7_output), .in_4(n2_bit_multiplexer_8_output),
    .Output(n2_bit_multiplexer_10_output), .Selector(in_33[3:2]));
  _1_bit_Multiplexer u_1_bit_multiplexer_1 (
    .i0(n2_bit_multiplexer_9_output), .i1(n2_bit_multiplexer_10_output), .out(Output), .Selector(in_33[4]));

  // Other names for the same wires on the sheet: _0_1[1:0] = in_33[1:0]; _2_3[1:0] = in_33[3:2]; _4 = in_33[4]
endmodule

module _1_bit_32_bit_Multiplexer (
  input  [31:0] i0,
  input  [31:0] i1,
  input  Selector,
  output [31:0] out
);

  wire [31:0] and_1_out, and_2_out;

  assign and_1_out = i0 & ~{32{Selector}};  // AND_Gate and_1, 32 bits wide
  assign and_2_out = i1 & {32{Selector}};  // AND_Gate and_2, 32 bits wide
  assign out = and_1_out | and_2_out;  // OR_Gate or_1, 32 bits wide
endmodule

module _2_bit_32_bit_Multiplexer (
  input  [31:0] in_1,
  input  [31:0] in_2,
  input  [31:0] in_3,
  input  [31:0] in_4,
  input  [1:0] Selector,
  output [31:0] Output
);

  wire [31:0] n1_bit_32_bit_multiplexer_1_out, n1_bit_32_bit_multiplexer_2_out;

  _1_bit_32_bit_Multiplexer u_1_bit_32_bit_multiplexer_1 (
    .i0(in_1), .i1(in_2), .out(n1_bit_32_bit_multiplexer_1_out), .Selector(Selector[0]));
  _1_bit_32_bit_Multiplexer u_1_bit_32_bit_multiplexer_2 (
    .i0(in_3), .i1(in_4), .out(n1_bit_32_bit_multiplexer_2_out), .Selector(Selector[0]));
  _1_bit_32_bit_Multiplexer u_1_bit_32_bit_multiplexer_3 (
    .i0(n1_bit_32_bit_multiplexer_1_out), .i1(n1_bit_32_bit_multiplexer_2_out), .out(Output),
    .Selector(Selector[1]));
endmodule

module _3_bit_32_bit_Multiplexer (
  input  [31:0] in_1,
  input  [31:0] in_2,
  input  [31:0] in_3,
  input  [31:0] in_4,
  input  [31:0] in_5,
  input  [31:0] in_6,
  input  [31:0] in_7,
  input  [31:0] in_8,
  input  [2:0] in_9,
  output [31:0] Output
);

  wire [31:0] n2_bit_32_bit_multiplexer_1_output, n2_bit_32_bit_multiplexer_2_output;

  _2_bit_32_bit_Multiplexer u_2_bit_32_bit_multiplexer_1 (
    .in_1(in_1), .in_2(in_2), .in_3(in_3), .in_4(in_4), .Output(n2_bit_32_bit_multiplexer_1_output),
    .Selector(in_9[1:0]));
  _2_bit_32_bit_Multiplexer u_2_bit_32_bit_multiplexer_2 (
    .in_1(in_5), .in_2(in_6), .in_3(in_7), .in_4(in_8), .Output(n2_bit_32_bit_multiplexer_2_output),
    .Selector(in_9[1:0]));
  _1_bit_32_bit_Multiplexer u_1_bit_32_bit_multiplexer_1 (
    .i0(n2_bit_32_bit_multiplexer_1_output), .i1(n2_bit_32_bit_multiplexer_2_output), .out(Output),
    .Selector(in_9[2]));
endmodule

module _4_bit_32_bit_Multiplexer (
  input  [31:0] in_1,
  input  [31:0] in_2,
  input  [31:0] in_3,
  input  [31:0] in_4,
  input  [31:0] in_5,
  input  [31:0] in_6,
  input  [31:0] in_7,
  input  [31:0] in_8,
  input  [31:0] in_9,
  input  [31:0] in_10,
  input  [31:0] in_11,
  input  [31:0] in_12,
  input  [31:0] in_13,
  input  [31:0] in_14,
  input  [31:0] in_15,
  input  [31:0] in_16,
  input  [3:0] in_17,
  output [31:0] Output
);

  wire [31:0] n3_bit_32_bit_multiplexer_1_output, n3_bit_32_bit_multiplexer_2_output;

  _3_bit_32_bit_Multiplexer u_3_bit_32_bit_multiplexer_1 (
    .in_1(in_1), .in_2(in_2), .in_3(in_3), .in_4(in_4), .in_5(in_5), .in_6(in_6), .in_7(in_7), .in_8(in_8),
    .Output(n3_bit_32_bit_multiplexer_1_output), .in_9(in_17[2:0]));
  _3_bit_32_bit_Multiplexer u_3_bit_32_bit_multiplexer_2 (
    .in_1(in_9), .in_2(in_10), .in_3(in_11), .in_4(in_12), .in_5(in_13), .in_6(in_14), .in_7(in_15),
    .in_8(in_16), .Output(n3_bit_32_bit_multiplexer_2_output), .in_9(in_17[2:0]));
  _1_bit_32_bit_Multiplexer u_1_bit_32_bit_multiplexer_1 (
    .i0(n3_bit_32_bit_multiplexer_1_output), .i1(n3_bit_32_bit_multiplexer_2_output), .out(Output),
    .Selector(in_17[3]));
endmodule

module _5_bit_32_bit_Multiplexer (
  input  [31:0] in_1,
  input  [31:0] in_2,
  input  [31:0] in_3,
  input  [31:0] in_4,
  input  [31:0] in_5,
  input  [31:0] in_6,
  input  [31:0] in_7,
  input  [31:0] in_8,
  input  [31:0] in_9,
  input  [31:0] in_10,
  input  [31:0] in_11,
  input  [31:0] in_12,
  input  [31:0] in_13,
  input  [31:0] in_14,
  input  [31:0] in_15,
  input  [31:0] in_16,
  input  [31:0] in_17,
  input  [31:0] in_18,
  input  [31:0] in_19,
  input  [31:0] in_20,
  input  [31:0] in_21,
  input  [31:0] in_22,
  input  [31:0] in_23,
  input  [31:0] in_24,
  input  [31:0] in_25,
  input  [31:0] in_26,
  input  [31:0] in_27,
  input  [31:0] in_28,
  input  [31:0] in_29,
  input  [31:0] in_30,
  input  [31:0] in_31,
  input  [31:0] in_32,
  input  [4:0] in_33,
  output [31:0] Output
);

  wire [31:0] n2_bit_32_bit_multiplexer_1_output, n2_bit_32_bit_multiplexer_2_output,
       n2_bit_32_bit_multiplexer_3_output, n2_bit_32_bit_multiplexer_4_output,
       n2_bit_32_bit_multiplexer_5_output, n2_bit_32_bit_multiplexer_6_output,
       n2_bit_32_bit_multiplexer_7_output, n2_bit_32_bit_multiplexer_8_output,
       n2_bit_32_bit_multiplexer_9_output, n2_bit_32_bit_multiplexer_10_output;

  _2_bit_32_bit_Multiplexer u_2_bit_32_bit_multiplexer_1 (
    .in_1(in_1), .in_2(in_2), .in_3(in_3), .in_4(in_4), .Output(n2_bit_32_bit_multiplexer_1_output),
    .Selector(in_33[1:0]));
  _2_bit_32_bit_Multiplexer u_2_bit_32_bit_multiplexer_2 (
    .in_1(in_5), .in_2(in_6), .in_3(in_7), .in_4(in_8), .Output(n2_bit_32_bit_multiplexer_2_output),
    .Selector(in_33[1:0]));
  _2_bit_32_bit_Multiplexer u_2_bit_32_bit_multiplexer_3 (
    .in_1(in_9), .in_2(in_10), .in_3(in_11), .in_4(in_12), .Output(n2_bit_32_bit_multiplexer_3_output),
    .Selector(in_33[1:0]));
  _2_bit_32_bit_Multiplexer u_2_bit_32_bit_multiplexer_4 (
    .in_1(in_13), .in_2(in_14), .in_3(in_15), .in_4(in_16), .Output(n2_bit_32_bit_multiplexer_4_output),
    .Selector(in_33[1:0]));
  _2_bit_32_bit_Multiplexer u_2_bit_32_bit_multiplexer_5 (
    .in_1(in_17), .in_2(in_18), .in_3(in_19), .in_4(in_20), .Output(n2_bit_32_bit_multiplexer_5_output),
    .Selector(in_33[1:0]));
  _2_bit_32_bit_Multiplexer u_2_bit_32_bit_multiplexer_6 (
    .in_1(in_21), .in_2(in_22), .in_3(in_23), .in_4(in_24), .Output(n2_bit_32_bit_multiplexer_6_output),
    .Selector(in_33[1:0]));
  _2_bit_32_bit_Multiplexer u_2_bit_32_bit_multiplexer_7 (
    .in_1(in_25), .in_2(in_26), .in_3(in_27), .in_4(in_28), .Output(n2_bit_32_bit_multiplexer_7_output),
    .Selector(in_33[1:0]));
  _2_bit_32_bit_Multiplexer u_2_bit_32_bit_multiplexer_8 (
    .in_1(in_29), .in_2(in_30), .in_3(in_31), .in_4(in_32), .Output(n2_bit_32_bit_multiplexer_8_output),
    .Selector(in_33[1:0]));
  _2_bit_32_bit_Multiplexer u_2_bit_32_bit_multiplexer_9 (
    .in_1(n2_bit_32_bit_multiplexer_1_output), .in_2(n2_bit_32_bit_multiplexer_2_output),
    .in_3(n2_bit_32_bit_multiplexer_3_output), .in_4(n2_bit_32_bit_multiplexer_4_output),
    .Output(n2_bit_32_bit_multiplexer_9_output), .Selector(in_33[3:2]));
  _2_bit_32_bit_Multiplexer u_2_bit_32_bit_multiplexer_10 (
    .in_1(n2_bit_32_bit_multiplexer_5_output), .in_2(n2_bit_32_bit_multiplexer_6_output),
    .in_3(n2_bit_32_bit_multiplexer_7_output), .in_4(n2_bit_32_bit_multiplexer_8_output),
    .Output(n2_bit_32_bit_multiplexer_10_output), .Selector(in_33[3:2]));
  _1_bit_32_bit_Multiplexer u_1_bit_32_bit_multiplexer_1 (
    .i0(n2_bit_32_bit_multiplexer_9_output), .i1(n2_bit_32_bit_multiplexer_10_output), .out(Output),
    .Selector(in_33[4]));

  // Other names for the same wires on the sheet: _0_1[1:0] = in_33[1:0]; _2_3[1:0] = in_33[3:2]; _4 = in_33[4]
endmodule

module _1_sbit_5_dbit_Multiplexer (
  input  [4:0] i0,
  input  [4:0] i1,
  input  Selector,
  output [4:0] out
);

  wire [4:0] and_1_out, and_2_out;

  assign and_1_out = i0 & ~{5{Selector}};  // AND_Gate and_1, 5 bits wide
  assign and_2_out = i1 & {5{Selector}};  // AND_Gate and_2, 5 bits wide
  assign out = and_1_out | and_2_out;  // OR_Gate or_1, 5 bits wide
endmodule

module _2_sbit_5_dbit_Multiplexer (
  input  [4:0] in_1,
  input  [4:0] in_2,
  input  [4:0] in_3,
  input  [4:0] in_4,
  input  [1:0] Selector,
  output [4:0] Output
);

  wire [4:0] n1_sbit_5_dbit_multiplexer_1_out, n1_sbit_5_dbit_multiplexer_2_out;

  _1_sbit_5_dbit_Multiplexer u_1_sbit_5_dbit_multiplexer_1 (
    .i0(in_1), .i1(in_2), .out(n1_sbit_5_dbit_multiplexer_1_out), .Selector(Selector[0]));
  _1_sbit_5_dbit_Multiplexer u_1_sbit_5_dbit_multiplexer_2 (
    .i0(in_3), .i1(in_4), .out(n1_sbit_5_dbit_multiplexer_2_out), .Selector(Selector[0]));
  _1_sbit_5_dbit_Multiplexer u_1_sbit_5_dbit_multiplexer_3 (
    .i0(n1_sbit_5_dbit_multiplexer_1_out), .i1(n1_sbit_5_dbit_multiplexer_2_out), .out(Output),
    .Selector(Selector[1]));
endmodule

module _1_bit_Demultiplexer (
  input  i,
  input  S,
  output o0,
  output o1
);

  and and_1 (o0, i, ~S);  // AND_Gate
  and and_2 (o1, i, S);
endmodule

module _2_bit_Demultiplexer (
  input  i,
  input  [1:0] S,
  output o0,
  output o1,
  output o2,
  output o3
);

  wire a0, a1, b0, b1;

  _1_bit_Demultiplexer u_1_bit_demultiplexer_1 (.i(i), .S(S[0]), .o0(a0), .o1(a1));
  _1_bit_Demultiplexer u_1_bit_demultiplexer_2 (.i(i), .S(S[1]), .o0(b0), .o1(b1));
  and and_1 (o0, a0, b0);
  and and_2 (o1, a1, b0);
  and and_3 (o2, a0, b1);
  and and_4 (o3, a1, b1);
endmodule

module _3_bit_Demultiplexer (
  input  i,
  input  [2:0] S,
  output o0,
  output o1,
  output o2,
  output o3,
  output o4,
  output o5,
  output o6,
  output o7
);

  wire _0_minus_minus, _1_minus_minus, minus_00, minus_01, minus_10, minus_11;

  _2_bit_Demultiplexer u_2_bit_demultiplexer_1 (
    .i(i), .S(S[1:0]), .o0(minus_00), .o1(minus_01), .o2(minus_10), .o3(minus_11));
  _1_bit_Demultiplexer u_1_bit_demultiplexer_1 (.i(i), .S(S[2]), .o0(_0_minus_minus), .o1(_1_minus_minus));
  and and_1 (o0, minus_00, _0_minus_minus);
  and and_2 (o1, minus_01, _0_minus_minus);
  and and_3 (o2, minus_10, _0_minus_minus);
  and and_4 (o3, minus_11, _0_minus_minus);
  and and_5 (o4, minus_00, _1_minus_minus);
  and and_6 (o5, minus_01, _1_minus_minus);
  and and_7 (o6, minus_10, _1_minus_minus);
  and and_8 (o7, minus_11, _1_minus_minus);
endmodule

module _4_bit_Demultiplexer (
  input  in,
  input  [3:0] Selector,
  output _0000,
  output _0001,
  output _0010,
  output _0011,
  output _0100,
  output _0101,
  output _0110,
  output _0111,
  output _1000,
  output _1001,
  output _1010,
  output _1011,
  output _1100,
  output _1101,
  output _1110,
  output _1111
);

  wire n1_bit_demultiplexer_1_o0, n1_bit_demultiplexer_1_o1;

  _1_bit_Demultiplexer u_1_bit_demultiplexer_1 (
    .i(in), .S(Selector[3]), .o0(n1_bit_demultiplexer_1_o0), .o1(n1_bit_demultiplexer_1_o1));
  _3_bit_Demultiplexer u_3_bit_demultiplexer_1 (
    .i(n1_bit_demultiplexer_1_o0), .S(Selector[2:0]), .o0(_0000), .o1(_0001), .o2(_0010), .o3(_0011),
    .o4(_0100), .o5(_0101), .o6(_0110), .o7(_0111));
  _3_bit_Demultiplexer u_3_bit_demultiplexer_2 (
    .i(n1_bit_demultiplexer_1_o1), .S(Selector[2:0]), .o0(_1000), .o1(_1001), .o2(_1010), .o3(_1011),
    .o4(_1100), .o5(_1101), .o6(_1110), .o7(_1111));
endmodule

module _5_bit_Demultiplexer (
  input  in,
  input  [4:0] Selector,
  output _00000,
  output _00001,
  output _00010,
  output _00011,
  output _00100,
  output _00101,
  output _00110,
  output _00111,
  output _01000,
  output _01001,
  output _01010,
  output _01011,
  output _01100,
  output _01101,
  output _01110,
  output _01111,
  output _10000,
  output _10001,
  output _10010,
  output _10011,
  output _10100,
  output _10101,
  output _10110,
  output _10111,
  output _11000,
  output _11001,
  output _11010,
  output _11011,
  output _11100,
  output _11101,
  output _11110,
  output _11111
);

  wire n1_bit_demultiplexer_1_o0, n1_bit_demultiplexer_1_o1;

  _1_bit_Demultiplexer u_1_bit_demultiplexer_1 (
    .i(in), .S(Selector[4]), .o0(n1_bit_demultiplexer_1_o0), .o1(n1_bit_demultiplexer_1_o1));
  _4_bit_Demultiplexer u_4_bit_demultiplexer_1 (
    .in(n1_bit_demultiplexer_1_o0), ._0000(_00000), ._0001(_00001), ._0010(_00010), ._0011(_00011),
    ._0100(_00100), ._0101(_00101), ._0110(_00110), ._0111(_00111), ._1000(_01000), ._1001(_01001),
    ._1010(_01010), ._1011(_01011), ._1100(_01100), ._1101(_01101), ._1110(_01110), ._1111(_01111),
    .Selector(Selector[3:0]));
  _4_bit_Demultiplexer u_4_bit_demultiplexer_2 (
    .in(n1_bit_demultiplexer_1_o1), ._0000(_10000), ._0001(_10001), ._0010(_10010), ._0011(_10011),
    ._0100(_10100), ._0101(_10101), ._0110(_10110), ._0111(_10111), ._1000(_11000), ._1001(_11001),
    ._1010(_11010), ._1011(_11011), ._1100(_11100), ._1101(_11101), ._1110(_11110), ._1111(_11111),
    .Selector(Selector[3:0]));
endmodule

module _1_sbit_5_dbit_Demux (
  input  [4:0] i,
  input  Selector,
  output [4:0] o0,
  output [4:0] o1
);

  assign o0 = i & ~{5{Selector}};  // AND_Gate and_1, 5 bits wide
  assign o1 = i & {5{Selector}};  // AND_Gate and_2, 5 bits wide
endmodule

module _1_sbit_32_dbit_Demux (
  input  [31:0] i,
  input  S,
  output [31:0] o0,
  output [31:0] o1
);

  assign o0 = i & ~{32{S}};  // AND_Gate and_1, 32 bits wide
  assign o1 = i & {32{S}};  // AND_Gate and_2, 32 bits wide
endmodule

module _2_sbit_32_dbit_Demux (
  input  [31:0] i,
  input  [1:0] S,
  output [31:0] o0,
  output [31:0] o1,
  output [31:0] o2,
  output [31:0] o3
);

  wire [31:0] a0, a1, b0, b1;

  _1_sbit_32_dbit_Demux u_1_sbit_32_dbit_demux_1 (.i(i), .S(S[0]), .o0(a0), .o1(a1));
  _1_sbit_32_dbit_Demux u_1_sbit_32_dbit_demux_2 (.i(i), .S(S[1]), .o0(b0), .o1(b1));
  assign o0 = a0 & b0;  // AND_Gate and_1, 32 bits wide
  assign o2 = a0 & b1;  // AND_Gate and_2, 32 bits wide
  assign o1 = a1 & b0;  // AND_Gate and_3, 32 bits wide
  assign o3 = a1 & b1;  // AND_Gate and_4, 32 bits wide
endmodule

module _3_sbit_32_dbit_Demux (
  input  [31:0] i,
  input  [2:0] S,
  output [31:0] o4,
  output [31:0] o0,
  output [31:0] o1,
  output [31:0] o5,
  output [31:0] o2,
  output [31:0] o6,
  output [31:0] o3,
  output [31:0] o7
);

  wire [31:0] _0_minus_minus, _1_minus_minus, minus_00, minus_01, minus_10, minus_11;

  _2_sbit_32_dbit_Demux u_2_sbit_32_dbit_demux_1 (
    .i(i), .S(S[1:0]), .o0(minus_00), .o1(minus_01), .o2(minus_10), .o3(minus_11));
  _1_sbit_32_dbit_Demux u_1_sbit_32_dbit_demux_1 (.i(i), .S(S[2]), .o0(_0_minus_minus), .o1(_1_minus_minus));
  assign o0 = minus_00 & _0_minus_minus;  // AND_Gate and_1, 32 bits wide
  assign o1 = minus_01 & _0_minus_minus;  // AND_Gate and_2, 32 bits wide
  assign o2 = minus_10 & _0_minus_minus;  // AND_Gate and_3, 32 bits wide
  assign o3 = minus_11 & _0_minus_minus;  // AND_Gate and_4, 32 bits wide
  assign o4 = minus_00 & _1_minus_minus;  // AND_Gate and_5, 32 bits wide
  assign o5 = minus_01 & _1_minus_minus;  // AND_Gate and_6, 32 bits wide
  assign o6 = minus_10 & _1_minus_minus;  // AND_Gate and_7, 32 bits wide
  assign o7 = minus_11 & _1_minus_minus;  // AND_Gate and_8, 32 bits wide
endmodule

module _4_sbit_32_dbit_Demux (
  input  [31:0] in,
  input  [3:0] Selector,
  output [31:0] _0000,
  output [31:0] _0001,
  output [31:0] _0010,
  output [31:0] _0011,
  output [31:0] _0100,
  output [31:0] _0101,
  output [31:0] _0110,
  output [31:0] _0111,
  output [31:0] _1000,
  output [31:0] _1001,
  output [31:0] _1010,
  output [31:0] _1011,
  output [31:0] _1100,
  output [31:0] _1101,
  output [31:0] _1110,
  output [31:0] _1111
);

  wire [31:0] n1_sbit_32_dbit_demux_1_o0, n1_sbit_32_dbit_demux_1_o1;

  _1_sbit_32_dbit_Demux u_1_sbit_32_dbit_demux_1 (
    .i(in), .S(Selector[3]), .o0(n1_sbit_32_dbit_demux_1_o0), .o1(n1_sbit_32_dbit_demux_1_o1));
  _3_sbit_32_dbit_Demux u_3_sbit_32_dbit_demux_1 (
    .i(n1_sbit_32_dbit_demux_1_o0), .S(Selector[2:0]), .o4(_0000), .o0(_0001), .o1(_0010), .o5(_0011),
    .o2(_0100), .o6(_0101), .o3(_0110), .o7(_0111));
  _3_sbit_32_dbit_Demux u_3_sbit_32_dbit_demux_2 (
    .i(n1_sbit_32_dbit_demux_1_o1), .S(Selector[2:0]), .o4(_1000), .o0(_1001), .o1(_1010), .o5(_1011),
    .o2(_1100), .o6(_1101), .o3(_1110), .o7(_1111));
endmodule

module _5_sbit_32_dbit_Demux (
  input  [31:0] in,
  input  [4:0] Selector,
  output [31:0] _00000,
  output [31:0] _00001,
  output [31:0] _00010,
  output [31:0] _00011,
  output [31:0] _00100,
  output [31:0] _00101,
  output [31:0] _00110,
  output [31:0] _00111,
  output [31:0] _01000,
  output [31:0] _01001,
  output [31:0] _01010,
  output [31:0] _01011,
  output [31:0] _01100,
  output [31:0] _01101,
  output [31:0] _01110,
  output [31:0] _01111,
  output [31:0] _10000,
  output [31:0] _10001,
  output [31:0] _10010,
  output [31:0] _10011,
  output [31:0] _10100,
  output [31:0] _10101,
  output [31:0] _10110,
  output [31:0] _10111,
  output [31:0] _11000,
  output [31:0] _11001,
  output [31:0] _11010,
  output [31:0] _11011,
  output [31:0] _11100,
  output [31:0] _11101,
  output [31:0] _11110,
  output [31:0] _11111
);

  wire [31:0] n1_sbit_32_dbit_demux_1_o0, n1_sbit_32_dbit_demux_1_o1;

  _1_sbit_32_dbit_Demux u_1_sbit_32_dbit_demux_1 (
    .i(in), .S(Selector[4]), .o0(n1_sbit_32_dbit_demux_1_o0), .o1(n1_sbit_32_dbit_demux_1_o1));
  _4_sbit_32_dbit_Demux u_4_sbit_32_dbit_demux_1 (
    .in(n1_sbit_32_dbit_demux_1_o0), ._0000(_00000), ._0001(_00001), ._0010(_00010), ._0011(_00011),
    ._0100(_00100), ._0101(_00101), ._0110(_00110), ._0111(_00111), ._1000(_01000), ._1001(_01001),
    ._1010(_01010), ._1011(_01011), ._1100(_01100), ._1101(_01101), ._1110(_01110), ._1111(_01111),
    .Selector(Selector[3:0]));
  _4_sbit_32_dbit_Demux u_4_sbit_32_dbit_demux_2 (
    .in(n1_sbit_32_dbit_demux_1_o1), ._0000(_10000), ._0001(_10001), ._0010(_10010), ._0011(_10011),
    ._0100(_10100), ._0101(_10101), ._0110(_10110), ._0111(_10111), ._1000(_11000), ._1001(_11001),
    ._1010(_11010), ._1011(_11011), ._1100(_11100), ._1101(_11101), ._1110(_11110), ._1111(_11111),
    .Selector(Selector[3:0]));
endmodule
